// Logisim project control.circ as structural Verilog: 15 circuits, main circuit main
module main (
  input  in_1,
  input  in_2,
  input  in_3
);

  wire _1_R2_num, _2_bne_beq, _2_equal, _3_bJump, _4_halt, and_2_out, and_3_out, and_4_out, bJump, clk,
       comparator_1_eq, comparator_2_eq, control_1_beq_bne, control_1_rd_only, control_1_sw,
       control_1_syscall, ex_mem_1_halt_2, ex_mem_1_rd_only_2, ex_mem_1_sw_2, halt, id_ex_1_rd_only_2,
       id_ex_1_sw_2, not_1_out, not_2_out, not_4_out, not_5_out, rd_only, switch, syscall, xnor_1_out;
  wire [1:0] _1_R1_num, _2_JumpOp, _2_Y_num, control_1_din_num, control_1_jumpop, control_1_w_num,
       control_1_y_num, Din_num, ex_mem_1_din_out, ex_mem_1_w__out, id_ex_1_din_out, id_ex_1_w__out, W_num;
  wire [3:0] _2_OP, control_1_op, register_2_q_2, register_2_q_3, register_2_q_4, register_2_q_5,
       register_2_q_6;
  wire [4:0] _4_rd, _4_rt, control_1_rs_base, control_1_rt, multiplexer_2_out, multiplexer_4_out,
       multiplexer_5_out;
  wire [9:0] bit_extender_1_out;
  wire [11:0] register_2_q;
  wire [15:0] bit_extender_6_out, shifter_2_out;
  wire [25:0] _2_Out26;
  wire [31:0] _3__pc_next, _4_PC_1, adder_1_out, adder_2_out, adder_3_out, alu_1_result, ALU_out,
       bit_extender_2_out, bit_extender_3_out, bit_extender_4_out, bit_extender_5_out, Counter_q,
       ex_mem_1_alu_out, ex_mem_1_ir_out, ex_mem_1_memin_2, ex_mem_1_pc_out, id_ex_1_memin_2, id_ex_1_pc_out,
       id_ex_1_re_d2_2, if_id_1_ir_out, if_id_1_pc_out, MEM_out, mem_wb_1_ir_out, mem_wb_1_pc_out,
       multiplexer_1_out, multiplexer_3_out, multiplexer_6_out, multiplexer_7_out, n32reg_1__0, n32reg_1__1,
       n32reg_1__2, n32reg_1__3, n32reg_1_r1, n32reg_1_r2, PC_NEXT, ram_1_data, RE_D1, register_1_q,
       rom_1_data, shifter_1_out;
  wire [31:26] id_ex_1_ir_out;

  Register #(.width(32)) register_1 (.D(multiplexer_1_out), .en(1'b1), .Q(register_1_q), .clk(clk), .clr(in_3));
  Multiplexer #(.width(32), .enable("false")) multiplexer_1 (
    .in0(adder_1_out), .in1(_3__pc_next), .out(multiplexer_1_out), .sel(_3_bJump));
  Bit_Extender #(.in_width(32), .out_width(10)) bit_extender_1 (.in(register_1_q), .out(bit_extender_1_out));
  Adder #(.width(32)) adder_1 (.a(register_1_q), .b(32'h1), .out(adder_1_out));  // open: cin, cout
  ROM #(.addrWidth(10), .dataWidth(32)) rom_1 (.addr(bit_extender_1_out), .data(rom_1_data), .sel(1'b1));
  IF_ID if_id_1 (
    .clk(clk), .PC(adder_1_out), .Instraction(rom_1_data), .PC_out(if_id_1_pc_out), .IR_out(if_id_1_ir_out));  // open: in_2
  // Probe on n32reg_1__0
  // Probe on n32reg_1__1
  // Probe on n32reg_1__2
  // Probe on n32reg_1__3
  Multiplexer #(.select(2), .width(5), .disabled(0), .enable("false")) multiplexer_2 (
    .in0(_4_rd), .in1(_4_rt), .in2({5{1'b1}}), .in3({5{1'b1}}), .out(multiplexer_2_out), .sel(W_num));
  Multiplexer #(.select(2), .width(32), .disabled(0), .enable("false")) multiplexer_3 (
    .in0(ALU_out), .in1(MEM_out), .in2(_4_PC_1), .in3(_4_PC_1), .out(multiplexer_3_out), .sel(Din_num));
  _32reg u_32reg_1 (
    ._0(n32reg_1__0), ._1(n32reg_1__1), ._2(n32reg_1__2), .R1(n32reg_1_r1), ._3(n32reg_1__3), .CLK(clk),
    .R2(n32reg_1_r2), .Din(multiplexer_3_out), .W_num(multiplexer_2_out), .WT_RD(not_1_out),
    .R1_num(multiplexer_4_out), .R2_num(multiplexer_5_out));
  not not_1 (not_1_out, rd_only);
  Control control_1 (
    .in_1(if_id_1_ir_out), .Y_num(control_1_y_num), .R1_num(_1_R1_num), .R2(_1_R2_num),
    .W_num(control_1_w_num), .Din_num(control_1_din_num), .OP(control_1_op), .JumpOp(control_1_jumpop),
    .beq_bne(control_1_beq_bne), .rs_base(control_1_rs_base), .rt(control_1_rt), .sw(control_1_sw),
    .rd_only(control_1_rd_only), .syscall(control_1_syscall));  // open: rd, sa, IMM_offset, Out26
  Multiplexer #(.select(2), .width(5), .disabled(0), .enable("false")) multiplexer_4 (
    .in0(control_1_rs_base), .in1(control_1_rt), .in2(5'b00010), .in3(5'b00010), .out(multiplexer_4_out),
    .sel(_1_R1_num));
  Multiplexer #(.width(5), .disabled(0), .enable("false")) multiplexer_5 (
    .in0(control_1_rt), .in1(5'b00100), .out(multiplexer_5_out), .sel(_1_R2_num));
  Register #(.width(32)) Counter (.D(adder_2_out), .en(1'b1), .Q(Counter_q), .clk(clk), .clr(in_1));
  // Probe on adder_2_out
  // Probe on n32reg_1_r1
  Clock clock_1 (.out(switch));
  Adder #(.width(32)) adder_2 (.a(Counter_q), .b(32'h1), .out(adder_2_out), .cin(1'b0));  // open: cout
  ID_Ex id_ex_1 (
    .clk(clk), .PC(if_id_1_pc_out), .PC_out(id_ex_1_pc_out), .IR_out({id_ex_1_ir_out, _2_Out26}),
    .Instraction(if_id_1_ir_out), .W_num(control_1_w_num), .W__out(id_ex_1_w__out),
    .Din_num(control_1_din_num), .Din_out(id_ex_1_din_out), .rd_only(control_1_rd_only),
    .rd_only_2(id_ex_1_rd_only_2), .MemIn(n32reg_1_r2), .MemIn_2(id_ex_1_memin_2), .sw(control_1_sw),
    .sw_2(id_ex_1_sw_2), .Y_num(control_1_y_num), .Y__out(_2_Y_num), .op(control_1_op), .op__out(_2_OP),
    .RE_D1(n32reg_1_r1), .RE_D2(n32reg_1_r2), .RE_D1_2(RE_D1), .RE_D2_2(id_ex_1_re_d2_2),
    .bne_beq(control_1_beq_bne), .bne_beq_2(_2_bne_beq), .Jump_op(control_1_jumpop), .Jump_op_2(_2_JumpOp),
    .syscall(control_1_syscall), .syscall_2(syscall));
  not not_2 (not_2_out, _4_halt);
  // Probe on _2_OP
  and and_1 (clk, switch, not_2_out);
  Comparator #(.width(2)) comparator_1 (.a(_2_JumpOp), .b(2'b00), .eq(comparator_1_eq));  // open: gt, lt
  Hex_Digit_Display hex_digit_display_1 (.value(register_2_q_6));  // open: dp
  assign bit_extender_2_out = {{27{1'b0}}, _2_Out26[10:6]};  // Bit_Extender bit_extender_2
  assign bit_extender_3_out = {{16{_2_Out26[15]}}, _2_Out26[15:0]};  // Bit_Extender bit_extender_3
  assign bit_extender_4_out = {{16{1'b0}}, _2_Out26[15:0]};  // Bit_Extender bit_extender_4
  assign bit_extender_5_out = {{16{1'b0}}, _2_Out26[15:0]};  // Bit_Extender bit_extender_5
  Adder #(.width(32)) adder_3 (
    .a(id_ex_1_pc_out), .b(bit_extender_5_out), .out(adder_3_out), .cin(1'b0));  // open: cout
  xnor xnor_1 (xnor_1_out, _2_bne_beq, _2_equal);
  and and_2 (and_2_out, _2_JumpOp[0], _2_JumpOp[1]);
  not not_3 (bJump, comparator_1_eq);
  Hex_Digit_Display hex_digit_display_2 (.value(register_2_q_5));  // open: dp
  Multiplexer #(.select(2), .width(32), .disabled(0), .enable("false")) multiplexer_6 (
    .in0(id_ex_1_re_d2_2), .in1(bit_extender_3_out), .in2(bit_extender_4_out), .in3(bit_extender_2_out),
    .out(multiplexer_6_out), .sel(_2_Y_num));
  Shifter #(.width(32), .shift("lr")) shifter_1 (
    .in({id_ex_1_pc_out[31:28], _2_Out26, 2'b00}), .\dist (5'b00010), .out(shifter_1_out));
  Multiplexer #(.width(32), .disabled(0), .enable("false")) multiplexer_7 (
    .in0(id_ex_1_pc_out), .in1(adder_3_out), .out(multiplexer_7_out), .sel(and_3_out));
  and and_3 (and_3_out, xnor_1_out, and_2_out);
  Hex_Digit_Display hex_digit_display_3 (.value(register_2_q_3));  // open: dp
  Hex_Digit_Display hex_digit_display_4 (.value(register_2_q_4));  // open: dp
  and and_4 (and_4_out, syscall, not_4_out);
  not not_4 (not_4_out, _4_halt);
  Hex_Digit_Display hex_digit_display_5 (.value(register_2_q_2));  // open: dp
  Register #(.width(32)) register_2 (
    .D(id_ex_1_re_d2_2), .en(and_4_out),
    .Q({register_2_q_6, register_2_q_5, register_2_q_4, register_2_q_3, register_2_q_2, register_2_q}),
    .clk(clk), .clr(in_2));
  ALU alu_1 (
    .AluOP(_2_OP), .X(RE_D1), .Equal(_2_equal), .Result(alu_1_result), .Y(multiplexer_6_out));  // open: Signed_Overflow, Result_2, UnSigned_Overflow
  Multiplexer #(.select(2), .width(32), .disabled(0), .enable("false")) multiplexer_8 (
    .in0(id_ex_1_pc_out), .in1(RE_D1), .in2(shifter_1_out), .in3(multiplexer_7_out), .out(PC_NEXT),
    .sel(_2_JumpOp));
  Comparator #(.width(32), .mode("unsigned")) comparator_2 (
    .a(RE_D1), .b(32'ha), .eq(comparator_2_eq));  // open: gt, lt
  and and_5 (halt, comparator_2_eq, syscall);
  Hex_Digit_Display hex_digit_display_6 (.value(register_2_q[11:8]));  // open: dp
  Hex_Digit_Display hex_digit_display_7 (.value(register_2_q[7:4]));  // open: dp
  Hex_Digit_Display hex_digit_display_8 (.value(register_2_q[3:0]));  // open: dp
  EX_MEM ex_mem_1 (
    .clk(clk), .PC(id_ex_1_pc_out), .PC_out(ex_mem_1_pc_out), .IR_out(ex_mem_1_ir_out),
    .Instraction({id_ex_1_ir_out, _2_Out26}), .W_num(id_ex_1_w__out), .W__out(ex_mem_1_w__out),
    .Din_num(id_ex_1_din_out), .Din_out(ex_mem_1_din_out), .rd_only(id_ex_1_rd_only_2),
    .rd_only_2(ex_mem_1_rd_only_2), .ALU(alu_1_result), .ALU_out(ex_mem_1_alu_out), .MemIn(id_ex_1_memin_2),
    .MemIn_2(ex_mem_1_memin_2), .sw(id_ex_1_sw_2), .sw_2(ex_mem_1_sw_2), .pc_next(PC_NEXT),
    .pc_next_2(_3__pc_next), .bJump(bJump), .bJump_2(_3_bJump), .halt(halt), .halt_2(ex_mem_1_halt_2));
  Bit_Extender #(.in_width(32)) bit_extender_6 (.in(ex_mem_1_alu_out), .out(bit_extender_6_out));
  Shifter #(.width(16), .shift("lr")) shifter_2 (.in(bit_extender_6_out), .\dist (4'b0010), .out(shifter_2_out));
  RAM #(.addrWidth(16), .dataWidth(32)) ram_1 (
    .addr(shifter_2_out), .data(ram_1_data), .sel(1'b1), .clk(clk), .ld(not_5_out), .clr(1'b0));
  not not_5 (not_5_out, ex_mem_1_sw_2);
  assign ram_1_data = ex_mem_1_sw_2 ? ex_mem_1_memin_2 : 32'bz;  // Controlled_Buffer controlled_buffer_1
  MEM_WB mem_wb_1 (
    .clk(clk), .PC(ex_mem_1_pc_out), .Instraction(ex_mem_1_ir_out), .W_num(ex_mem_1_w__out),
    .Din_num(ex_mem_1_din_out), .rd_only(ex_mem_1_rd_only_2), .PC_out(mem_wb_1_pc_out),
    .IR_out({mem_wb_1_ir_out[31:21], _4_rt, _4_rd, mem_wb_1_ir_out[10:0]}), .W__out(W_num),
    .Din_out(Din_num), .rd_only_2(rd_only), .ALU(ex_mem_1_alu_out), .ALU_out(ALU_out), .MEM(ram_1_data),
    .MEM_out(MEM_out), .halt(ex_mem_1_halt_2), .halt_2(_4_halt));
  Adder #(.width(32)) adder_4 (.a(mem_wb_1_pc_out), .b({32{1'b0}}), .out(_4_PC_1), .cin(1'b0));  // open: cout

  // Notes on the sheet:
  //   contents of rom_1 (hex, n*v repeats v):
  //   20100000 20110000 20120000 20130000 36100000 36310001 36520002 36730003 ae100000 ae110004 ae120008
  //   ae13000c 2002000a 20110000 20120000 20130000 c
  //   Mem
  //   JAL
  //   a0
  //   v0
  //   PC
  //   PC+1
  //   sa
  //   offset
  //   RE.D1
  //   RE.D2
  //   JUMP
  //   RE.D1
  //   AluRes
  //   ALUres
  //   sw
endmodule

module Control (
  input  [31:0] in_1,
  output [1:0] Y_num,
  output sw,
  output rd_only,
  output syscall,
  output [1:0] R1_num,
  output R2,
  output [1:0] W_num,
  output [1:0] Din_num,
  output [3:0] OP,
  output [1:0] JumpOp,
  output beq_bne,
  output [4:0] rs_base,
  output [4:0] rt,
  output [4:0] rd,
  output [4:0] sa,
  output [15:0] IMM_offset,
  output [25:0] Out26
);

  wire specialchoice_1_j;
  wire [5:0] specialchoice_1_out;

  SpecialChoice specialchoice_1 (.Hi6(in_1[31:26]), .Lo6(in_1[5:0]), .J(specialchoice_1_j), .Out(specialchoice_1_out));
  Y_Choice y_choice_1 (
    .j(specialchoice_1_j), .a(specialchoice_1_out[5]), .b(specialchoice_1_out[4]),
    .c(specialchoice_1_out[3]), .d(specialchoice_1_out[2]), .e(specialchoice_1_out[1]),
    .f(specialchoice_1_out[0]), .o1(Y_num[1]), .o2(Y_num[0]));
  R1_Mux r1_mux_1 (
    .j(specialchoice_1_j), .a(specialchoice_1_out[5]), .b(specialchoice_1_out[4]), .o(R1_num[0]),
    .c(specialchoice_1_out[3]), .d(specialchoice_1_out[2]), .e(specialchoice_1_out[1]),
    .f(specialchoice_1_out[0]), .o_v0(R1_num[1]));
  R2 r2_1 (
    .j(specialchoice_1_j), .a(specialchoice_1_out[5]), .b(specialchoice_1_out[4]),
    .c(specialchoice_1_out[3]), .d(specialchoice_1_out[2]), .e(specialchoice_1_out[1]),
    .f(specialchoice_1_out[0]), .o1(R2));
  W_Mux w_mux_1 (
    .j(specialchoice_1_j), .a(specialchoice_1_out[5]), .b(specialchoice_1_out[4]),
    .c(specialchoice_1_out[3]), .o1(W_num[0]), .d(specialchoice_1_out[2]), .e(specialchoice_1_out[1]),
    .f(specialchoice_1_out[0]), .o2(W_num[1]));
  Din_Mux din_mux_1 (
    .j(specialchoice_1_j), .a(specialchoice_1_out[5]), .o1(Din_num[0]), .b(specialchoice_1_out[4]),
    .c(specialchoice_1_out[3]), .d(specialchoice_1_out[2]), .o2_H(Din_num[1]), .e(specialchoice_1_out[1]),
    .f(specialchoice_1_out[0]));
  OPchoice opchoice_1 (
    .j(specialchoice_1_j), .a(specialchoice_1_out[5]), .b(specialchoice_1_out[4]),
    .c(specialchoice_1_out[3]), .d(specialchoice_1_out[2]), .e(specialchoice_1_out[1]),
    .f(specialchoice_1_out[0]), .o1(OP[3]), .o2(OP[2]), .o3(OP[1]), .o4(OP[0]));
  JUMP jump_1 (
    .j(specialchoice_1_j), .a(specialchoice_1_out[5]), .b(specialchoice_1_out[4]),
    .c(specialchoice_1_out[3]), .d(specialchoice_1_out[2]), .op1(JumpOp[0]), .e(specialchoice_1_out[1]),
    .f(specialchoice_1_out[0]), .op2(JumpOp[1]), .beq_bne(beq_bne));
  Signal signal_1 (
    .j(specialchoice_1_j), .a(specialchoice_1_out[5]), .b(specialchoice_1_out[4]),
    .c(specialchoice_1_out[3]), .d(specialchoice_1_out[2]), .e(specialchoice_1_out[1]),
    .f(specialchoice_1_out[0]), .sw(sw), .rd_reg(rd_only), .syscall(syscall));

  assign IMM_offset = in_1[15:0];
  assign Out26 = in_1[25:0];
  assign rd = in_1[15:11];
  assign rs_base = in_1[25:21];
  assign rt = in_1[20:16];
  assign sa = in_1[10:6];
endmodule

module R1_Mux (
  input  j,
  input  a,
  input  b,
  input  c,
  input  d,
  input  e,
  input  f,
  output o,
  output o_v0
);

  wire and_1_out, and_2_out, not_1_out, not_2_out, not_3_out, not_4_out, not_5_out, not_6_out, not_7_out,
       not_8_out, not_9_out, not_10_out, not_11_out, not_12_out, not_13_out;

  not not_1 (not_1_out, a);
  not not_2 (not_2_out, b);
  not not_3 (not_3_out, c);
  not not_4 (not_4_out, d);
  not not_5 (not_5_out, f);
  not not_6 (not_6_out, a);
  not not_7 (not_7_out, b);
  not not_8 (not_8_out, c);
  not not_9 (not_9_out, d);
  not not_10 (not_10_out, a);
  not not_11 (not_11_out, b);
  not not_12 (not_12_out, e);
  not not_13 (not_13_out, f);
  and and_1 (and_1_out, j, not_1_out, not_2_out, not_3_out, not_4_out, not_5_out);
  and and_2 (and_2_out, j, not_6_out, not_7_out, not_8_out, not_9_out, e);
  and and_3 (o_v0, j, not_10_out, not_11_out, c, d, not_12_out, not_13_out);
  or or_1 (o, and_1_out, and_2_out);
endmodule

module SpecialChoice (
  input  [5:0] Hi6,
  input  [5:0] Lo6,
  output J,
  output [5:0] Out
);

  wire not_2_out, not_3_out, not_4_out, not_5_out, not_6_out, not_7_out;
  wire [5:0] and_1_out, and_2_out, bit_extender_1_out, not_1_out;

  assign not_1_out = ~bit_extender_1_out;  // NOT_Gate not_1, 6 bits wide
  assign and_1_out = not_1_out & Hi6;  // AND_Gate and_1, 6 bits wide
  assign and_2_out = bit_extender_1_out & Lo6;  // AND_Gate and_2, 6 bits wide
  not not_2 (not_2_out, Hi6[0]);
  not not_3 (not_3_out, Hi6[1]);
  not not_4 (not_4_out, Hi6[2]);
  not not_5 (not_5_out, Hi6[3]);
  not not_6 (not_6_out, Hi6[4]);
  not not_7 (not_7_out, Hi6[5]);
  and and_3 (J, not_2_out, not_3_out, not_4_out, not_5_out, not_6_out, not_7_out);
  assign Out = and_1_out | and_2_out;  // OR_Gate or_1, 6 bits wide
  assign bit_extender_1_out = {{5{J}}, J};  // Bit_Extender bit_extender_1
endmodule

module W_Mux (
  input  j,
  input  a,
  input  b,
  input  c,
  input  d,
  input  e,
  input  f,
  output o1,
  output o2
);

  wire and_1_out, and_2_out, and_3_out, not_1_out, not_2_out, not_3_out, not_4_out, not_5_out, not_6_out,
       not_7_out, not_8_out, not_9_out, not_10_out, not_11_out, not_12_out, not_13_out, not_14_out,
       not_15_out, not_16_out, not_17_out, not_18_out;

  not not_1 (not_1_out, j);
  not not_2 (not_2_out, a);
  not not_3 (not_3_out, b);
  not not_4 (not_4_out, d);
  not not_5 (not_5_out, f);
  not not_6 (not_6_out, j);
  not not_7 (not_7_out, a);
  not not_8 (not_8_out, b);
  not not_9 (not_9_out, e);
  not not_10 (not_10_out, j);
  not not_11 (not_11_out, b);
  not not_12 (not_12_out, c);
  not not_13 (not_13_out, d);
  not not_14 (not_14_out, j);
  not not_15 (not_15_out, a);
  not not_16 (not_16_out, b);
  not not_17 (not_17_out, c);
  not not_18 (not_18_out, d);
  and and_1 (and_1_out, not_1_out, not_2_out, not_3_out, c, not_4_out, not_5_out);
  and and_2 (and_2_out, not_6_out, not_7_out, not_8_out, c, not_9_out);
  and and_3 (and_3_out, not_10_out, a, not_11_out, not_12_out, not_13_out, e, f);
  and and_4 (o2, not_14_out, not_15_out, not_16_out, not_17_out, not_18_out, e, f);
  or or_1 (o1, and_1_out, and_2_out, and_3_out);
endmodule

module Din_Mux (
  input  j,
  input  a,
  input  b,
  input  c,
  input  d,
  input  e,
  input  f,
  output o1,
  output o2_H
);

  wire not_1_out, not_2_out, not_3_out, not_4_out, not_5_out, not_6_out, not_7_out, not_8_out, not_9_out;

  not not_1 (not_1_out, j);
  not not_2 (not_2_out, b);
  not not_3 (not_3_out, c);
  not not_4 (not_4_out, d);
  not not_5 (not_5_out, j);
  not not_6 (not_6_out, a);
  not not_7 (not_7_out, b);
  not not_8 (not_8_out, c);
  not not_9 (not_9_out, d);
  and and_1 (o1, not_1_out, a, not_2_out, not_3_out, not_4_out, e, f);
  and and_2 (o2_H, not_5_out, not_6_out, not_7_out, not_8_out, not_9_out, e, f);
endmodule

module Y_Choice (
  input  j,
  input  a,
  input  b,
  input  c,
  input  d,
  input  e,
  input  f,
  output o1,
  output o2
);

  wire and_1_out, and_2_out, and_3_out, and_4_out, and_5_out, and_6_out, and_7_out, and_8_out, not_1_out,
       not_2_out, not_3_out, not_4_out, not_5_out, not_6_out, not_7_out, not_8_out, not_9_out, not_10_out,
       not_11_out, not_12_out, not_13_out, not_14_out, not_15_out, not_16_out, not_17_out, not_18_out,
       not_19_out, not_20_out, not_21_out, not_22_out, not_23_out, not_24_out, not_25_out, not_26_out,
       not_27_out, not_28_out, not_29_out, not_30_out, not_31_out, not_32_out, not_33_out, not_34_out,
       not_35_out;

  not not_1 (not_1_out, j);
  not not_2 (not_2_out, a);
  not not_3 (not_3_out, b);
  not not_4 (not_4_out, e);
  not not_5 (not_5_out, a);
  not not_6 (not_6_out, b);
  not not_7 (not_7_out, c);
  not not_8 (not_8_out, d);
  not not_9 (not_9_out, f);
  not not_10 (not_10_out, a);
  not not_11 (not_11_out, b);
  not not_12 (not_12_out, c);
  not not_13 (not_13_out, d);
  not not_14 (not_14_out, j);
  not not_15 (not_15_out, a);
  not not_16 (not_16_out, b);
  not not_17 (not_17_out, d);
  not not_18 (not_18_out, e);
  not not_19 (not_19_out, j);
  not not_20 (not_20_out, a);
  not not_21 (not_21_out, b);
  not not_22 (not_22_out, d);
  not not_23 (not_23_out, f);
  not not_24 (not_24_out, j);
  not not_25 (not_25_out, b);
  not not_26 (not_26_out, d);
  not not_27 (not_27_out, a);
  not not_28 (not_28_out, b);
  not not_29 (not_29_out, c);
  not not_30 (not_30_out, d);
  not not_31 (not_31_out, f);
  not not_32 (not_32_out, a);
  not not_33 (not_33_out, b);
  not not_34 (not_34_out, c);
  not not_35 (not_35_out, d);
  and and_1 (and_1_out, not_1_out, not_2_out, not_3_out, c, d, not_4_out);
  and and_2 (and_2_out, j, not_5_out, not_6_out, not_7_out, not_8_out, not_9_out);
  and and_3 (and_3_out, j, not_10_out, not_11_out, not_12_out, not_13_out, e);
  and and_4 (and_4_out, not_14_out, not_15_out, not_16_out, c, not_17_out, not_18_out);
  and and_5 (and_5_out, not_19_out, not_20_out, not_21_out, c, not_22_out, not_23_out);
  and and_6 (and_6_out, not_24_out, a, not_25_out, not_26_out, e, f);
  and and_7 (and_7_out, j, not_27_out, not_28_out, not_29_out, not_30_out, not_31_out);
  and and_8 (and_8_out, j, not_32_out, not_33_out, not_34_out, not_35_out, e);
  or or_1 (o1, and_1_out, and_2_out, and_3_out);
  or or_2 (o2, and_4_out, and_5_out, and_6_out, and_7_out, and_8_out);

  // Notes on the sheet:
  //   o1 o2
  //   RE.D2 00 
  //   S   01
  //   Z   10
  //   sa   11
endmodule

module OPchoice (
  input  j,
  input  a,
  input  b,
  input  c,
  input  d,
  input  e,
  input  f,
  output o1,
  output o2,
  output o3,
  output o4
);

  wire and_1_out, and_2_out, and_3_out, and_4_out, and_5_out, and_6_out, and_7_out, and_8_out, and_9_out,
       and_10_out, and_11_out, and_12_out, and_13_out, and_14_out, and_15_out, and_16_out, and_17_out,
       and_18_out, and_19_out, and_20_out, and_21_out, and_22_out, and_23_out, and_24_out, and_25_out,
       and_26_out, and_27_out, and_28_out, and_29_out, and_30_out, and_31_out, and_32_out, and_33_out,
       and_34_out, not_1_out, not_2_out, not_3_out, not_4_out, not_5_out, not_6_out, not_7_out, not_8_out,
       not_9_out, not_10_out, not_11_out, not_12_out, not_13_out, not_14_out, not_15_out, not_16_out,
       not_17_out, not_18_out, not_19_out, not_20_out, not_21_out, not_22_out, not_23_out, not_24_out,
       not_25_out, not_26_out, not_27_out, not_28_out, not_29_out, not_30_out, not_31_out, not_32_out,
       not_33_out, not_34_out, not_35_out, not_36_out, not_37_out, not_38_out, not_39_out, not_40_out,
       not_41_out, not_42_out, not_43_out, not_44_out, not_45_out, not_46_out, not_47_out, not_48_out,
       not_49_out, not_50_out, not_51_out, not_52_out, not_53_out, not_54_out, not_55_out, not_56_out,
       not_57_out, not_58_out, not_59_out, not_60_out, not_61_out, not_62_out, not_63_out, not_64_out,
       not_65_out, not_66_out, not_67_out, not_68_out, not_69_out, not_70_out, not_71_out, not_72_out,
       not_73_out, not_74_out, not_75_out, not_76_out, not_77_out, not_78_out, not_79_out, not_80_out,
       not_81_out, not_82_out, not_83_out, not_84_out, not_85_out, not_86_out, not_87_out, not_88_out,
       not_89_out, not_90_out, not_91_out, not_92_out, not_93_out, not_94_out, not_95_out, not_96_out,
       not_97_out, not_98_out, not_99_out, not_100_out, not_101_out, not_102_out, not_103_out, not_104_out,
       not_105_out, not_106_out, not_107_out, not_108_out, not_109_out, not_110_out, not_111_out,
       not_112_out, not_113_out, not_114_out, not_115_out, not_116_out, not_117_out, not_118_out,
       not_119_out, not_120_out, not_121_out, not_122_out, not_123_out, not_124_out, not_125_out,
       not_126_out, not_127_out, not_128_out, not_129_out, not_130_out, not_131_out, not_132_out,
       not_133_out, not_134_out, not_135_out, not_136_out, not_137_out;

  not not_1 (not_1_out, b);
  not not_2 (not_2_out, c);
  not not_3 (not_3_out, e);
  not not_4 (not_4_out, j);
  not not_5 (not_5_out, a);
  not not_6 (not_6_out, b);
  not not_7 (not_7_out, e);
  not not_8 (not_8_out, b);
  not not_9 (not_9_out, c);
  not not_10 (not_10_out, b);
  not not_11 (not_11_out, d);
  not not_12 (not_12_out, f);
  not not_13 (not_13_out, j);
  not not_14 (not_14_out, a);
  not not_15 (not_15_out, b);
  not not_16 (not_16_out, d);
  not not_17 (not_17_out, f);
  not not_18 (not_18_out, b);
  not not_19 (not_19_out, d);
  not not_20 (not_20_out, b);
  not not_21 (not_21_out, c);
  not not_22 (not_22_out, d);
  not not_23 (not_23_out, e);
  not not_24 (not_24_out, f);
  not not_25 (not_25_out, j);
  not not_26 (not_26_out, a);
  not not_27 (not_27_out, b);
  not not_28 (not_28_out, d);
  not not_29 (not_29_out, e);
  not not_30 (not_30_out, f);
  not not_31 (not_31_out, j);
  not not_32 (not_32_out, a);
  not not_33 (not_33_out, b);
  not not_34 (not_34_out, d);
  not not_35 (not_35_out, e);
  not not_36 (not_36_out, b);
  not not_37 (not_37_out, c);
  not not_38 (not_38_out, d);
  not not_39 (not_39_out, e);
  not not_40 (not_40_out, b);
  not not_41 (not_41_out, c);
  not not_42 (not_42_out, e);
  not not_43 (not_43_out, f);
  not not_44 (not_44_out, j);
  not not_45 (not_45_out, a);
  not not_46 (not_46_out, b);
  not not_47 (not_47_out, e);
  not not_48 (not_48_out, f);
  not not_49 (not_49_out, b);
  not not_50 (not_50_out, c);
  not not_51 (not_51_out, d);
  not not_52 (not_52_out, f);
  not not_53 (not_53_out, j);
  not not_54 (not_54_out, b);
  not not_55 (not_55_out, c);
  not not_56 (not_56_out, d);
  not not_57 (not_57_out, j);
  not not_58 (not_58_out, b);
  not not_59 (not_59_out, d);
  not not_60 (not_60_out, b);
  not not_61 (not_61_out, d);
  not not_62 (not_62_out, b);
  not not_63 (not_63_out, c);
  not not_64 (not_64_out, e);
  not not_65 (not_65_out, f);
  not not_66 (not_66_out, j);
  not not_67 (not_67_out, a);
  not not_68 (not_68_out, b);
  not not_69 (not_69_out, e);
  not not_70 (not_70_out, f);
  not not_71 (not_71_out, a);
  not not_72 (not_72_out, b);
  not not_73 (not_73_out, c);
  not not_74 (not_74_out, d);
  not not_75 (not_75_out, b);
  not not_76 (not_76_out, c);
  not not_77 (not_77_out, d);
  not not_78 (not_78_out, f);
  not not_79 (not_79_out, b);
  not not_80 (not_80_out, c);
  not not_81 (not_81_out, b);
  not not_82 (not_82_out, d);
  not not_83 (not_83_out, f);
  not not_84 (not_84_out, j);
  not not_85 (not_85_out, a);
  not not_86 (not_86_out, b);
  not not_87 (not_87_out, d);
  not not_88 (not_88_out, f);
  not not_89 (not_89_out, b);
  not not_90 (not_90_out, c);
  not not_91 (not_91_out, d);
  not not_92 (not_92_out, e);
  not not_93 (not_93_out, f);
  not not_94 (not_94_out, j);
  not not_95 (not_95_out, a);
  not not_96 (not_96_out, b);
  not not_97 (not_97_out, d);
  not not_98 (not_98_out, e);
  not not_99 (not_99_out, f);
  not not_100 (not_100_out, j);
  not not_101 (not_101_out, a);
  not not_102 (not_102_out, b);
  not not_103 (not_103_out, d);
  not not_104 (not_104_out, e);
  not not_105 (not_105_out, b);
  not not_106 (not_106_out, c);
  not not_107 (not_107_out, d);
  not not_108 (not_108_out, e);
  not not_109 (not_109_out, b);
  not not_110 (not_110_out, c);
  not not_111 (not_111_out, e);
  not not_112 (not_112_out, f);
  not not_113 (not_113_out, j);
  not not_114 (not_114_out, a);
  not not_115 (not_115_out, b);
  not not_116 (not_116_out, e);
  not not_117 (not_117_out, f);
  not not_118 (not_118_out, a);
  not not_119 (not_119_out, b);
  not not_120 (not_120_out, c);
  not not_121 (not_121_out, d);
  not not_122 (not_122_out, f);
  not not_123 (not_123_out, j);
  not not_124 (not_124_out, b);
  not not_125 (not_125_out, c);
  not not_126 (not_126_out, d);
  not not_127 (not_127_out, j);
  not not_128 (not_128_out, b);
  not not_129 (not_129_out, d);
  not not_130 (not_130_out, b);
  not not_131 (not_131_out, d);
  not not_132 (not_132_out, f);
  not not_133 (not_133_out, j);
  not not_134 (not_134_out, a);
  not not_135 (not_135_out, b);
  not not_136 (not_136_out, d);
  not not_137 (not_137_out, f);
  and and_1 (and_1_out, j, a, not_1_out, not_2_out, d, not_3_out, f);
  and and_2 (and_2_out, not_4_out, not_5_out, not_6_out, c, d, not_7_out, f);
  and and_3 (and_3_out, j, a, not_8_out, not_9_out, d, e, f);
  and and_4 (and_4_out, j, a, not_10_out, c, not_11_out, e, not_12_out);
  and and_5 (and_5_out, not_13_out, not_14_out, not_15_out, c, not_16_out, e, not_17_out);
  and and_6 (and_6_out, j, a, not_18_out, c, not_19_out, e, f);
  and and_7 (and_7_out, j, a, not_20_out, not_21_out, not_22_out, not_23_out, not_24_out);
  and and_8 (and_8_out, not_25_out, not_26_out, not_27_out, c, not_28_out, not_29_out, not_30_out);
  and and_9 (and_9_out, not_31_out, not_32_out, not_33_out, c, not_34_out, not_35_out, f);
  and and_10 (and_10_out, j, a, not_36_out, not_37_out, not_38_out, not_39_out, f);
  and and_11 (and_11_out, j, a, not_40_out, not_41_out, d, not_42_out, not_43_out);
  and and_12 (and_12_out, not_44_out, not_45_out, not_46_out, c, d, not_47_out, not_48_out);
  and and_13 (and_13_out, j, a, not_49_out, not_50_out, not_51_out, e, not_52_out);
  and and_14 (and_14_out, not_53_out, a, not_54_out, not_55_out, not_56_out, e, f);
  and and_15 (and_15_out, not_57_out, a, not_58_out, c, not_59_out, e, f);
  and and_16 (and_16_out, j, a, not_60_out, c, not_61_out, e, f);
  and and_17 (and_17_out, j, a, not_62_out, not_63_out, d, not_64_out, not_65_out);
  and and_18 (and_18_out, not_66_out, not_67_out, not_68_out, c, d, not_69_out, not_70_out);
  and and_19 (and_19_out, j, not_71_out, not_72_out, not_73_out, not_74_out, e, f);
  and and_20 (and_20_out, j, a, not_75_out, not_76_out, not_77_out, e, not_78_out);
  and and_21 (and_21_out, j, a, not_79_out, not_80_out, d, e, f);
  and and_22 (and_22_out, j, a, not_81_out, c, not_82_out, e, not_83_out);
  and and_23 (and_23_out, not_84_out, not_85_out, not_86_out, c, not_87_out, e, not_88_out);
  and and_24 (and_24_out, j, a, not_89_out, not_90_out, not_91_out, not_92_out, not_93_out);
  and and_25 (and_25_out, not_94_out, not_95_out, not_96_out, c, not_97_out, not_98_out, not_99_out);
  and and_26 (and_26_out, not_100_out, not_101_out, not_102_out, c, not_103_out, not_104_out, f);
  and and_27 (and_27_out, j, a, not_105_out, not_106_out, not_107_out, not_108_out, f);
  and and_28 (and_28_out, j, a, not_109_out, not_110_out, d, not_111_out, not_112_out);
  and and_29 (and_29_out, not_113_out, not_114_out, not_115_out, c, d, not_116_out, not_117_out);
  and and_30 (and_30_out, j, not_118_out, not_119_out, not_120_out, not_121_out, e, not_122_out);
  and and_31 (and_31_out, not_123_out, a, not_124_out, not_125_out, not_126_out, e, f);
  and and_32 (and_32_out, not_127_out, a, not_128_out, c, not_129_out, e, f);
  and and_33 (and_33_out, j, a, not_130_out, c, not_131_out, e, not_132_out);
  and and_34 (and_34_out, not_133_out, not_134_out, not_135_out, c, not_136_out, e, not_137_out);
  or or_1 (o1, and_1_out, and_2_out, and_3_out, and_4_out, and_5_out, and_6_out);
  or or_2 (o2, and_7_out, and_8_out, and_9_out, and_10_out, and_11_out, and_12_out, and_13_out, and_14_out, and_15_out, and_16_out);
  or or_3 (o3, and_17_out, and_18_out, and_19_out, and_20_out, and_21_out, and_22_out, and_23_out);
  or or_4 (o4, and_24_out, and_25_out, and_26_out, and_27_out, and_28_out, and_29_out, and_30_out, and_31_out, and_32_out, and_33_out, and_34_out);
endmodule

module JUMP (
  input  j,
  input  a,
  input  b,
  input  c,
  input  d,
  input  e,
  input  f,
  output op1,
  output op2,
  output beq_bne
);

  wire and_1_out, and_2_out, and_3_out, and_4_out, and_5_out, and_6_out, and_7_out, not_1_out, not_2_out,
       not_3_out, not_4_out, not_5_out, not_6_out, not_7_out, not_8_out, not_9_out, not_10_out, not_11_out,
       not_12_out, not_13_out, not_14_out, not_15_out, not_16_out, not_17_out, not_18_out, not_19_out,
       not_20_out, not_21_out, not_22_out, not_23_out, not_24_out, not_25_out, not_26_out, not_27_out,
       not_28_out, not_29_out, not_30_out, not_31_out, not_32_out, not_33_out, not_34_out, not_35_out,
       not_36_out, not_37_out, not_38_out, not_39_out, not_40_out, not_41_out, not_42_out, not_43_out,
       not_44_out;

  not not_1 (not_1_out, a);
  not not_2 (not_2_out, b);
  not not_3 (not_3_out, d);
  not not_4 (not_4_out, e);
  not not_5 (not_5_out, f);
  not not_6 (not_6_out, j);
  not not_7 (not_7_out, a);
  not not_8 (not_8_out, b);
  not not_9 (not_9_out, c);
  not not_10 (not_10_out, e);
  not not_11 (not_11_out, f);
  not not_12 (not_12_out, j);
  not not_13 (not_13_out, a);
  not not_14 (not_14_out, b);
  not not_15 (not_15_out, c);
  not not_16 (not_16_out, e);
  not not_17 (not_17_out, j);
  not not_18 (not_18_out, a);
  not not_19 (not_19_out, b);
  not not_20 (not_20_out, c);
  not not_21 (not_21_out, d);
  not not_22 (not_22_out, f);
  not not_23 (not_23_out, j);
  not not_24 (not_24_out, a);
  not not_25 (not_25_out, b);
  not not_26 (not_26_out, c);
  not not_27 (not_27_out, d);
  not not_28 (not_28_out, j);
  not not_29 (not_29_out, a);
  not not_30 (not_30_out, b);
  not not_31 (not_31_out, c);
  not not_32 (not_32_out, e);
  not not_33 (not_33_out, f);
  not not_34 (not_34_out, j);
  not not_35 (not_35_out, a);
  not not_36 (not_36_out, b);
  not not_37 (not_37_out, c);
  not not_38 (not_38_out, e);
  not not_39 (not_39_out, j);
  not not_40 (not_40_out, a);
  not not_41 (not_41_out, b);
  not not_42 (not_42_out, c);
  not not_43 (not_43_out, e);
  not not_44 (not_44_out, f);
  and and_1 (and_1_out, j, not_1_out, not_2_out, c, not_3_out, not_4_out, not_5_out);
  and and_2 (and_2_out, not_6_out, not_7_out, not_8_out, not_9_out, d, not_10_out, not_11_out);
  and and_3 (and_3_out, not_12_out, not_13_out, not_14_out, not_15_out, d, not_16_out, f);
  and and_4 (and_4_out, not_17_out, not_18_out, not_19_out, not_20_out, not_21_out, e, not_22_out);
  and and_5 (and_5_out, not_23_out, not_24_out, not_25_out, not_26_out, not_27_out, e, f);
  and and_6 (and_6_out, not_28_out, not_29_out, not_30_out, not_31_out, d, not_32_out, not_33_out);
  and and_7 (and_7_out, not_34_out, not_35_out, not_36_out, not_37_out, d, not_38_out, f);
  and and_8 (beq_bne, not_39_out, not_40_out, not_41_out, not_42_out, d, not_43_out, not_44_out);
  or or_1 (op1, and_1_out, and_2_out, and_3_out);
  or or_2 (op2, and_4_out, and_5_out, and_6_out, and_7_out);
endmodule

module R2 (
  input  j,
  input  a,
  input  b,
  input  c,
  input  d,
  input  e,
  input  f,
  output o1
);

  wire not_1_out, not_2_out, not_3_out, not_4_out;

  not not_1 (not_1_out, a);
  not not_2 (not_2_out, b);
  not not_3 (not_3_out, e);
  not not_4 (not_4_out, f);
  and and_1 (o1, j, not_1_out, not_2_out, c, d, not_3_out, not_4_out);
endmodule

module Signal (
  input  j,
  input  a,
  input  b,
  input  c,
  input  d,
  input  e,
  input  f,
  output sw,
  output rd_reg,
  output syscall
);

  wire and_2_out, and_3_out, and_4_out, and_5_out, and_6_out, and_7_out, and_8_out, and_9_out, not_1_out,
       not_2_out, not_3_out, not_4_out, not_5_out, not_6_out, not_7_out, not_8_out, not_9_out, not_10_out,
       not_11_out, not_12_out, not_13_out, not_14_out, not_15_out, not_16_out, not_17_out, not_18_out,
       not_19_out, not_20_out, not_21_out, not_22_out, not_23_out, not_24_out, not_25_out, not_26_out,
       not_27_out, not_28_out, not_29_out, not_30_out, not_31_out, not_32_out, not_33_out, not_34_out,
       not_35_out, not_36_out, not_37_out, not_38_out, not_39_out, not_40_out, not_41_out, not_42_out,
       not_43_out, not_44_out, not_45_out, not_46_out, not_47_out, not_48_out;

  not not_1 (not_1_out, j);
  not not_2 (not_2_out, b);
  not not_3 (not_3_out, d);
  not not_4 (not_4_out, j);
  not not_5 (not_5_out, b);
  not not_6 (not_6_out, d);
  not not_7 (not_7_out, j);
  not not_8 (not_8_out, a);
  not not_9 (not_9_out, b);
  not not_10 (not_10_out, c);
  not not_11 (not_11_out, e);
  not not_12 (not_12_out, f);
  not not_13 (not_13_out, j);
  not not_14 (not_14_out, a);
  not not_15 (not_15_out, b);
  not not_16 (not_16_out, c);
  not not_17 (not_17_out, e);
  not not_18 (not_18_out, j);
  not not_19 (not_19_out, a);
  not not_20 (not_20_out, b);
  not not_21 (not_21_out, c);
  not not_22 (not_22_out, d);
  not not_23 (not_23_out, f);
  not not_24 (not_24_out, a);
  not not_25 (not_25_out, b);
  not not_26 (not_26_out, d);
  not not_27 (not_27_out, e);
  not not_28 (not_28_out, f);
  not not_29 (not_29_out, a);
  not not_30 (not_30_out, b);
  not not_31 (not_31_out, e);
  not not_32 (not_32_out, f);
  not not_33 (not_33_out, j);
  not not_34 (not_34_out, a);
  not not_35 (not_35_out, c);
  not not_36 (not_36_out, d);
  not not_37 (not_37_out, e);
  not not_38 (not_38_out, f);
  not not_39 (not_39_out, j);
  not not_40 (not_40_out, a);
  not not_41 (not_41_out, c);
  not not_42 (not_42_out, d);
  not not_43 (not_43_out, e);
  not not_44 (not_44_out, f);
  not not_45 (not_45_out, a);
  not not_46 (not_46_out, b);
  not not_47 (not_47_out, e);
  not not_48 (not_48_out, f);
  and and_1 (sw, not_1_out, a, not_2_out, c, not_3_out, e, f);
  and and_2 (and_2_out, not_4_out, a, not_5_out, c, not_6_out, e, f);
  and and_3 (and_3_out, not_7_out, not_8_out, not_9_out, not_10_out, d, not_11_out, not_12_out);
  and and_4 (and_4_out, not_13_out, not_14_out, not_15_out, not_16_out, d, not_17_out, f);
  and and_5 (and_5_out, not_18_out, not_19_out, not_20_out, not_21_out, not_22_out, e, not_23_out);
  and and_6 (and_6_out, j, not_24_out, not_25_out, c, not_26_out, not_27_out, not_28_out);
  and and_7 (and_7_out, j, not_29_out, not_30_out, c, d, not_31_out, not_32_out);
  and and_8 (and_8_out, not_33_out, not_34_out, b, not_35_out, not_36_out, not_37_out, not_38_out);
  and and_9 (and_9_out, not_39_out, not_40_out, b, not_41_out, not_42_out, not_43_out, not_44_out);
  and and_10 (syscall, j, not_45_out, not_46_out, c, d, not_47_out, not_48_out);
  or or_1 (rd_reg, and_2_out, and_3_out, and_4_out, and_5_out, and_6_out, and_7_out, and_8_out, and_9_out);
endmodule

module IF_ID (
  input  clk,
  input  in_2,
  input  [31:0] PC,
  input  [31:0] Instraction,
  output [31:0] PC_out,
  output [31:0] IR_out
);

  Register #(.width(32)) PC_reg (.D(PC), .en(1'b1), .Q(PC_out), .clk(clk), .clr(in_2));
  Register #(.width(32)) IR (.D(Instraction), .en(1'b1), .Q(IR_out), .clk(clk), .clr(in_2));
endmodule

module ID_Ex (
  input  clk,
  input  [31:0] PC,
  input  [31:0] Instraction,
  input  [1:0] W_num,
  input  [1:0] Din_num,
  input  rd_only,
  input  [31:0] MemIn,
  input  sw,
  input  [1:0] Y_num,
  input  [3:0] op,
  input  [31:0] RE_D1,
  input  [31:0] RE_D2,
  input  bne_beq,
  input  [1:0] Jump_op,
  input  syscall,
  output [31:0] PC_out,
  output [31:0] IR_out,
  output [1:0] W__out,
  output [1:0] Din_out,
  output rd_only_2,
  output [31:0] MemIn_2,
  output sw_2,
  output [1:0] Y__out,
  output [3:0] op__out,
  output [31:0] RE_D1_2,
  output [31:0] RE_D2_2,
  output bne_beq_2,
  output [1:0] Jump_op_2,
  output syscall_2
);

  Register #(.width(32)) PC_reg (.D(PC), .en(1'b1), .Q(PC_out), .clk(clk), .clr(1'b0));
  Register #(.width(32)) IR (.D(Instraction), .en(1'b1), .Q(IR_out), .clk(clk), .clr(1'b0));
  Register #(.width(2)) W (.D(W_num), .en(1'b1), .Q(W__out), .clk(clk), .clr(1'b0));
  Register #(.width(2)) Din (.D(Din_num), .en(1'b1), .Q(Din_out), .clk(clk), .clr(1'b0));
  Register #(.width(1)) Din_2 (.D(rd_only), .en(1'b1), .Q(rd_only_2), .clk(clk), .clr(1'b0));
  Register #(.width(32)) mem (.D(MemIn), .en(1'b1), .Q(MemIn_2), .clk(clk), .clr(1'b0));
  Register #(.width(1)) register_1 (.D(sw), .en(1'b1), .Q(sw_2), .clk(clk), .clr(1'b0));
  Register #(.width(2)) register_2 (.D(Y_num), .en(1'b1), .Q(Y__out), .clk(clk), .clr(1'b0));
  Register #(.width(4)) u_op (.D(op), .en(1'b1), .Q(op__out), .clk(clk), .clr(1'b0));
  Register #(.width(32)) register_3 (.D(RE_D1), .en(1'b1), .Q(RE_D1_2), .clk(clk), .clr(1'b0));
  Register #(.width(32)) register_4 (.D(RE_D2), .en(1'b1), .Q(RE_D2_2), .clk(clk), .clr(1'b0));
  Register #(.width(1)) register_5 (.D(bne_beq), .en(1'b1), .Q(bne_beq_2), .clk(clk), .clr(1'b0));
  Register #(.width(2)) register_6 (.D(Jump_op), .en(1'b1), .Q(Jump_op_2), .clk(clk), .clr(1'b0));
  Register #(.width(1)) register_7 (.D(syscall), .en(1'b1), .Q(syscall_2), .clk(clk), .clr(1'b0));
endmodule

module EX_MEM (
  input  clk,
  input  [31:0] PC,
  input  [31:0] Instraction,
  input  [1:0] W_num,
  input  [1:0] Din_num,
  input  rd_only,
  input  [31:0] ALU,
  input  [31:0] MemIn,
  input  sw,
  input  [31:0] pc_next,
  input  bJump,
  input  halt,
  output [31:0] PC_out,
  output [31:0] IR_out,
  output [1:0] W__out,
  output [1:0] Din_out,
  output rd_only_2,
  output [31:0] ALU_out,
  output [31:0] MemIn_2,
  output sw_2,
  output [31:0] pc_next_2,
  output bJump_2,
  output halt_2
);

  Register #(.width(32)) PC_reg (.D(PC), .en(1'b1), .Q(PC_out), .clk(clk), .clr(1'b0));
  Register #(.width(32)) IR (.D(Instraction), .en(1'b1), .Q(IR_out), .clk(clk), .clr(1'b0));
  Register #(.width(2)) W (.D(W_num), .en(1'b1), .Q(W__out), .clk(clk), .clr(1'b0));
  Register #(.width(2)) Din (.D(Din_num), .en(1'b1), .Q(Din_out), .clk(clk), .clr(1'b0));
  Register #(.width(1)) Din_2 (.D(rd_only), .en(1'b1), .Q(rd_only_2), .clk(clk), .clr(1'b0));
  Register #(.width(32)) u_ALu (.D(ALU), .en(1'b1), .Q(ALU_out), .clk(clk), .clr(1'b0));
  Register #(.width(32)) mem (.D(MemIn), .en(1'b1), .Q(MemIn_2), .clk(clk), .clr(1'b0));
  Register #(.width(1)) register_1 (.D(sw), .en(1'b1), .Q(sw_2), .clk(clk), .clr(1'b0));
  Register #(.width(32)) register_2 (.D(pc_next), .en(1'b1), .Q(pc_next_2), .clk(clk), .clr(1'b0));
  Register #(.width(1)) register_3 (.D(bJump), .en(1'b1), .Q(bJump_2), .clk(clk), .clr(1'b0));
  Register #(.width(1)) register_4 (.D(halt), .en(1'b1), .Q(halt_2), .clk(clk), .clr(1'b0));
endmodule

module MEM_WB (
  input  clk,
  input  [31:0] PC,
  input  [31:0] Instraction,
  input  [1:0] W_num,
  input  [1:0] Din_num,
  input  rd_only,
  input  [31:0] ALU,
  input  [31:0] MEM,
  input  halt,
  output [31:0] PC_out,
  output [31:0] IR_out,
  output [1:0] W__out,
  output [1:0] Din_out,
  output rd_only_2,
  output [31:0] ALU_out,
  output [31:0] MEM_out,
  output halt_2
);

  Register #(.width(32)) PC_reg (.D(PC), .en(1'b1), .Q(PC_out), .clk(clk), .clr(1'b0));
  Register #(.width(32)) IR (.D(Instraction), .en(1'b1), .Q(IR_out), .clk(clk), .clr(1'b0));
  Register #(.width(2)) W (.D(W_num), .en(1'b1), .Q(W__out), .clk(clk), .clr(1'b0));
  Register #(.width(2)) Din (.D(Din_num), .en(1'b1), .Q(Din_out), .clk(clk), .clr(1'b0));
  Register #(.width(1)) Din_2 (.D(rd_only), .en(1'b1), .Q(rd_only_2), .clk(clk), .clr(1'b0));
  Register #(.width(32)) u_ALu (.D(ALU), .en(1'b1), .Q(ALU_out), .clk(clk), .clr(1'b0));
  Register #(.width(32)) ALu_2 (.D(MEM), .en(1'b1), .Q(MEM_out), .clk(clk), .clr(1'b0));
  Register #(.width(1)) Din_3 (.D(halt), .en(1'b1), .Q(halt_2), .clk(clk), .clr(1'b0));
endmodule
