// Logisim project 数据重定向(cuowu).circ as structural Verilog: 17 circuits, main circuit main
module main (
  input  in_1,
  input  in_2,
  input  in_3,
  input  in_4,
  input  in_5,
  input  in_6
);

  wire _1, _1_R2_num, _1_sw, _2_bLW, _2_bne_beq, _2_equal, _2_rd_only, _3_bLW, _3_rd_only, _4_halt,
       and_2_out, and_4_out, and_5_out, and_6_out, and_7_out, B_sucess, bJump, clk, comparator_1_eq,
       comparator_2_eq, control_1_beq_bne, control_1_rd_only, control_1_syscall, Data, DataInsert,
       ex_mem_1_halt_2, ex_mem_1_sw_2, id_ex_1_sw_2, judgedataargue_1_b_2_choice, judgedataargue_1_bmemchoic,
       MemChoice, not_1_out, not_2_out, not_3_out, not_4_out, not_5_out, not_6_out, nR1, nR2, or_1_out,
       rd_only, register_3_q, switch, syscall, xnor_1_out;
  wire [1:0] _1_R1_num, _2_JumpOp, _2_Y_num, _X_num, _Y_num, control_1_din_num, control_1_jumpop,
       control_1_w_num, control_1_y_num, Din_num, ex_mem_1_din_out, ex_mem_1_w__out, id_ex_1_din_out,
       id_ex_1_w__out, judgedataargue_1_r1_choice, judgedataargue_1_r2_choice, W_num;
  wire [3:0] _2_OP, control_1_op, register_5_q_2, register_5_q_3, register_5_q_4, register_5_q_5,
       register_5_q_6;
  wire [4:0] _2_W_reg, _3_W_reg, _4_rd, _4_rt, control_1_rs_base, control_1_rt, multiplexer_2_out,
       multiplexer_4_out, multiplexer_5_out;
  wire [9:0] bit_extender_1_out;
  wire [11:0] register_5_q;
  wire [15:0] bit_extender_6_out, shifter_2_out;
  wire [25:0] _2_Out26;
  wire [31:0] _3_sw_data, _4_PC_1, adder_1_out, adder_2_out, adder_3_out, adder_4_out, adder_5_out,
       adder_6_out, alu_1_result, ALU_out, bit_extender_2_out, bit_extender_3_out, bit_extender_4_out,
       bit_extender_5_out, buff1, buff3, BUFF4, buff4_t, Counter_2_q, Counter_3_q, Counter_4_q, Counter_q,
       ex_mem_1_memin_2, ex_mem_1_pc_out, id_ex_1_memin_2, id_ex_1_pc_out, id_ex_1_re_d1_2, id_ex_1_re_d2_2,
       if_id_1_pc_out, MEM_out, mem_wb_1_pc_out, multiplexer_1_out, multiplexer_6_out, multiplexer_7_out,
       multiplexer_8_out, multiplexer_9_out, multiplexer_11_out, multiplexer_12_out, n32reg_1__0,
       n32reg_1__1, n32reg_1__2, n32reg_1__3, n32reg_1_r1, n32reg_1_r2, PC_NEXT, ram_1_data, register_1_q,
       rom_1_data, shifter_1_out;
  wire [31:26] buff2;

  Clock clock_1 (.out(switch));
  // Probe on multiplexer_1_out
  Register #(.width(32)) register_1 (.D(multiplexer_1_out), .en(or_1_out), .Q(register_1_q), .clk(clk), .clr(in_2));
  Multiplexer #(.width(32), .enable("false")) multiplexer_1 (
    .in0(adder_1_out), .in1(PC_NEXT), .out(multiplexer_1_out), .sel(bJump));
  Bit_Extender #(.in_width(32), .out_width(10)) bit_extender_1 (.in(register_1_q), .out(bit_extender_1_out));
  // Probe on buff1
  // Probe on {buff2, _2_Out26}
  // Probe on buff3
  // Probe on {buff4_t[31:21], _4_rt, _4_rd, buff4_t[10:0]}
  // Probe on adder_4_out
  // Probe on Counter_q
  // Probe on Counter_2_q
  Register #(.width(32)) Counter (.D(adder_2_out), .en(B_sucess), .Q(Counter_q), .clk(clk), .clr(in_3));
  Register #(.width(32)) Counter_2 (.D(adder_3_out), .en(bJump), .Q(Counter_2_q), .clk(clk), .clr(in_4));
  Register #(.width(32)) Counter_3 (.D(adder_4_out), .en(1'b1), .Q(Counter_3_q), .clk(clk), .clr(in_5));
  Register #(.width(32)) Counter_4 (.D(adder_5_out), .en(Data), .Q(Counter_4_q), .clk(clk), .clr(in_6));
  not not_1 (not_1_out, _4_halt);
  // Probe on PC_NEXT
  Adder #(.width(32)) adder_1 (.a(register_1_q), .b(32'h1), .out(adder_1_out));  // open: cin, cout
  Adder #(.width(32)) adder_2 (.a(Counter_q), .b(32'h1), .out(adder_2_out), .cin(1'b0));  // open: cout
  Adder #(.width(32)) adder_3 (.a(Counter_2_q), .b(32'h1), .out(adder_3_out), .cin(1'b0));  // open: cout
  Adder #(.width(32)) adder_4 (.a(Counter_3_q), .b(32'h1), .out(adder_4_out), .cin(1'b0));  // open: cout
  Adder #(.width(32)) adder_5 (.a(Counter_4_q), .b(32'h1), .out(adder_5_out), .cin(1'b0));  // open: cout
  and and_1 (clk, switch, not_1_out);
  ROM #(.addrWidth(10), .dataWidth(32)) rom_1 (.addr(bit_extender_1_out), .data(rom_1_data), .sel(1'b1));
  // Probe on Counter_4_q
  not not_2 (not_2_out, Data);
  or or_1 (or_1_out, bJump, not_2_out);
  // Probe on multiplexer_2_out
  // Probe on BUFF4
  IF_ID if_id_1 (
    .clk(clk), .PC(adder_1_out), .Instraction(rom_1_data), .PC_out(if_id_1_pc_out), .IR_out(buff1),
    .Set0(bJump), .Keep(or_1_out));
  // Probe on n32reg_1__0
  // Probe on n32reg_1__1
  // Probe on n32reg_1__2
  // Probe on n32reg_1__3
  Multiplexer #(.select(2), .width(5), .disabled(0), .enable("false")) multiplexer_2 (
    .in0(_4_rd), .in1(_4_rt), .in2({5{1'b1}}), .in3({5{1'b1}}), .out(multiplexer_2_out), .sel(W_num));
  Multiplexer #(.select(2), .width(32), .disabled(0), .enable("false")) multiplexer_3 (
    .in0(ALU_out), .in1(MEM_out), .in2(_4_PC_1), .in3(_4_PC_1), .out(BUFF4), .sel(Din_num));
  _32reg u_32reg_1 (
    ._0(n32reg_1__0), ._1(n32reg_1__1), ._2(n32reg_1__2), .R1(n32reg_1_r1), ._3(n32reg_1__3), .CLK(clk),
    .R2(n32reg_1_r2), .Din(BUFF4), .W_num(multiplexer_2_out), .WT_RD(not_3_out), .R1_num(multiplexer_4_out),
    .R2_num(multiplexer_5_out));
  not not_3 (not_3_out, rd_only);
  Control control_1 (
    .in_1(buff1), .Y_num(control_1_y_num), .R1_num(_1_R1_num), .R2(_1_R2_num), .W_num(control_1_w_num),
    .Din_num(control_1_din_num), .OP(control_1_op), .JumpOp(control_1_jumpop), .beq_bne(control_1_beq_bne),
    .rs_base(control_1_rs_base), .rt(control_1_rt), .sw(_1_sw), .rd_only(control_1_rd_only),
    .syscall(control_1_syscall), .R1NoUse(nR1), .R2NoUse(nR2));  // open: rd, sa, IMM_offset, Out26
  Multiplexer #(.select(2), .width(5), .disabled(0), .enable("false")) multiplexer_4 (
    .in0(control_1_rs_base), .in1(control_1_rt), .in2(5'b00010), .in3(5'b00010), .out(multiplexer_4_out),
    .sel(_1_R1_num));
  Multiplexer #(.width(5), .disabled(0), .enable("false")) multiplexer_5 (
    .in0(control_1_rt), .in1(5'b00100), .out(multiplexer_5_out), .sel(_1_R2_num));
  JudgeDataArgue judgedataargue_1 (
    .R1(multiplexer_4_out), .R2(multiplexer_5_out), ._2_W(_2_W_reg), ._3_W(_3_W_reg), ._2_rd(_2_rd_only),
    ._3_rd(_3_rd_only), .R1NoUse(nR1), .R2NoUse(nR2), .R1_Choice(judgedataargue_1_r1_choice),
    .R2_Choice(judgedataargue_1_r2_choice), ._2_bLW(_2_bLW), .Load_Use(Data), .bSW(_1_sw),
    .bMemChoic(judgedataargue_1_bmemchoic), .b_2_choice(judgedataargue_1_b_2_choice));
  // Probe on n32reg_1_r2
  Register #(.width(1)) register_2 (.D(judgedataargue_1_b_2_choice), .Q(_1), .clk(clk));  // open: en, clr
  // Probe on judgedataargue_1_r2_choice
  // Probe on judgedataargue_1_r1_choice
  Register #(.width(1)) register_3 (.D(judgedataargue_1_bmemchoic), .Q(register_3_q), .clk(clk));  // open: en, clr
  Register #(.width(1)) register_4 (.D(register_3_q), .Q(MemChoice), .clk(clk));  // open: en, clr
  or or_2 (DataInsert, Data, bJump);
  ID_Ex id_ex_1 (
    .clk(clk), .PC(if_id_1_pc_out), .PC_out(id_ex_1_pc_out), .IR_out({buff2, _2_Out26}), .Instraction(buff1),
    .W_num(control_1_w_num), .W__out(id_ex_1_w__out), .Din_num(control_1_din_num), .Din_out(id_ex_1_din_out),
    .rd_only(control_1_rd_only), .rd_only_2(_2_rd_only), .MemIn(n32reg_1_r2), .MemIn_2(id_ex_1_memin_2),
    .sw(_1_sw), .sw_2(id_ex_1_sw_2), .Y_num(control_1_y_num), .Y__out(_2_Y_num), .op(control_1_op),
    .op__out(_2_OP), .RE_D1(n32reg_1_r1), .RE_D2(n32reg_1_r2), .RE_D1_2(id_ex_1_re_d1_2),
    .RE_D2_2(id_ex_1_re_d2_2), .bne_beq(control_1_beq_bne), .bne_beq_2(_2_bne_beq),
    .Jump_op(control_1_jumpop), .Jump_op_2(_2_JumpOp), .syscall(control_1_syscall), .syscall_2(syscall),
    .Set0(DataInsert), .X_num(judgedataargue_1_r1_choice), .X(_X_num), .Y_num_2(judgedataargue_1_r2_choice),
    .Y(_Y_num));
  W_Choice w_choice_1 (.IR({buff2, _2_Out26}), .in_2(id_ex_1_w__out), .W__out(_2_W_reg), .lw(_2_bLW));
  xnor xnor_1 (xnor_1_out, _2_bne_beq, _2_equal);
  and and_2 (and_2_out, _2_JumpOp[0], _2_JumpOp[1]);
  Comparator #(.width(2)) comparator_1 (.a(2'b00), .b(_2_JumpOp), .eq(comparator_1_eq));  // open: gt, lt
  Hex_Digit_Display hex_digit_display_1 (.value(register_5_q_6));  // open: dp
  assign bit_extender_2_out = {{27{1'b0}}, _2_Out26[10:6]};  // Bit_Extender bit_extender_2
  assign bit_extender_3_out = {{16{_2_Out26[15]}}, _2_Out26[15:0]};  // Bit_Extender bit_extender_3
  assign bit_extender_4_out = {{16{1'b0}}, _2_Out26[15:0]};  // Bit_Extender bit_extender_4
  assign bit_extender_5_out = {{16{1'b0}}, _2_Out26[15:0]};  // Bit_Extender bit_extender_5
  Adder #(.width(32)) adder_6 (
    .a(id_ex_1_pc_out), .b(bit_extender_5_out), .out(adder_6_out), .cin(1'b0));  // open: cout
  and and_3 (B_sucess, xnor_1_out, and_2_out);
  not not_4 (not_4_out, B_sucess);
  Hex_Digit_Display hex_digit_display_2 (.value(register_5_q_5));  // open: dp
  Multiplexer #(.select(2), .width(32), .disabled(0), .enable("false")) multiplexer_6 (
    .in0(id_ex_1_re_d2_2), .in1(bit_extender_3_out), .in2(bit_extender_4_out), .in3(bit_extender_2_out),
    .out(multiplexer_6_out), .sel(_2_Y_num));
  Shifter #(.width(32), .shift("lr")) shifter_1 (
    .in({id_ex_1_pc_out[31:28], _2_Out26, 2'b00}), .\dist (5'b00010), .out(shifter_1_out));
  Multiplexer #(.width(32), .disabled(0), .enable("false")) multiplexer_7 (
    .in0(id_ex_1_pc_out), .in1(adder_6_out), .out(multiplexer_7_out), .sel(B_sucess));
  and and_4 (and_4_out, not_4_out, and_2_out);
  Hex_Digit_Display hex_digit_display_3 (.value(register_5_q_3));  // open: dp
  Hex_Digit_Display hex_digit_display_4 (.value(register_5_q_4));  // open: dp
  and and_5 (and_5_out, syscall, not_5_out);
  not not_5 (not_5_out, _4_halt);
  nor nor_1 (bJump, and_4_out, comparator_1_eq);
  Hex_Digit_Display hex_digit_display_5 (.value(register_5_q_2));  // open: dp
  Register #(.width(32)) register_5 (
    .D(id_ex_1_re_d2_2), .en(and_5_out),
    .Q({register_5_q_6, register_5_q_5, register_5_q_4, register_5_q_3, register_5_q_2, register_5_q}),
    .clk(clk), .clr(in_1));
  Multiplexer #(.select(2), .width(32), .disabled(0), .enable("false")) multiplexer_8 (
    .in0(id_ex_1_re_d1_2), .in1(id_ex_1_re_d1_2), .in2(_3_sw_data), .in3(BUFF4), .out(multiplexer_8_out),
    .sel(_X_num));
  ALU alu_1 (
    .AluOP(_2_OP), .X(multiplexer_8_out), .Equal(_2_equal), .Result(alu_1_result), .Y(multiplexer_9_out));  // open: Signed_Overflow, Result_2, UnSigned_Overflow
  Multiplexer #(.select(2), .width(32), .disabled(0), .enable("false")) multiplexer_9 (
    .in0(multiplexer_6_out), .in1(multiplexer_6_out), .in2(_3_sw_data), .in3(BUFF4), .out(multiplexer_9_out),
    .sel(_Y_num));
  Multiplexer #(.select(2), .width(32), .disabled(0), .enable("false")) multiplexer_10 (
    .in0(id_ex_1_pc_out), .in1(multiplexer_8_out), .in2(shifter_1_out), .in3(multiplexer_7_out),
    .out(PC_NEXT), .sel(_2_JumpOp));
  Hex_Digit_Display hex_digit_display_6 (.value(register_5_q[7:4]));  // open: dp
  Hex_Digit_Display hex_digit_display_7 (.value(register_5_q[11:8]));  // open: dp
  Comparator #(.width(32), .mode("unsigned")) comparator_2 (
    .a(multiplexer_8_out), .b(32'ha), .eq(comparator_2_eq));  // open: gt, lt
  Hex_Digit_Display hex_digit_display_8 (.value(register_5_q[3:0]));  // open: dp
  and and_6 (and_6_out, comparator_2_eq, syscall);
  EX_MEM ex_mem_1 (
    .clk(clk), .PC(id_ex_1_pc_out), .PC_out(ex_mem_1_pc_out), .IR_out(buff3),
    .Instraction({buff2, _2_Out26}), .W_num(id_ex_1_w__out), .W__out(ex_mem_1_w__out),
    .Din_num(id_ex_1_din_out), .Din_out(ex_mem_1_din_out), .rd_only(_2_rd_only), .rd_only_2(_3_rd_only),
    .ALU(alu_1_result), .ALU_out(_3_sw_data), .MemIn(multiplexer_11_out), .MemIn_2(ex_mem_1_memin_2),
    .sw(id_ex_1_sw_2), .sw_2(ex_mem_1_sw_2), .halt(and_6_out), .halt_2(ex_mem_1_halt_2));
  Multiplexer #(.width(32), .enable("false")) multiplexer_11 (
    .in0(id_ex_1_memin_2), .in1(ALU_out), .out(multiplexer_11_out), .sel(_1));
  W_Choice w_choice_2 (.IR(buff3), .in_2(ex_mem_1_w__out), .W__out(_3_W_reg), .lw(_3_bLW));
  Bit_Extender #(.in_width(32)) bit_extender_6 (.in(_3_sw_data), .out(bit_extender_6_out));
  Shifter #(.width(16), .shift("lr")) shifter_2 (.in(bit_extender_6_out), .\dist (4'b0010), .out(shifter_2_out));
  not not_6 (not_6_out, ex_mem_1_sw_2);
  RAM #(.addrWidth(16), .dataWidth(32)) ram_1 (
    .addr(shifter_2_out), .data(ram_1_data), .sel(1'b1), .clk(clk), .ld(not_6_out), .clr(1'b0));
  assign ram_1_data = ex_mem_1_sw_2 ? multiplexer_12_out : 32'bz;  // Controlled_Buffer controlled_buffer_1
  MEM_WB mem_wb_1 (
    .clk(clk), .PC(ex_mem_1_pc_out), .Instraction(buff3), .W_num(ex_mem_1_w__out),
    .Din_num(ex_mem_1_din_out), .rd_only(_3_rd_only), .PC_out(mem_wb_1_pc_out),
    .IR_out({buff4_t[31:21], _4_rt, _4_rd, buff4_t[10:0]}), .W__out(W_num), .Din_out(Din_num),
    .rd_only_2(rd_only), .ALU(_3_sw_data), .ALU_out(ALU_out), .MEM(ram_1_data), .MEM_out(MEM_out),
    .halt(ex_mem_1_halt_2), .halt_2(_4_halt));
  Multiplexer #(.width(32), .enable("false")) multiplexer_12 (
    .in0(ex_mem_1_memin_2), .in1(ALU_out), .out(multiplexer_12_out), .sel(and_7_out));
  and and_7 (and_7_out, ex_mem_1_sw_2, MemChoice);
  Adder #(.width(32)) adder_7 (.a(mem_wb_1_pc_out), .b({32{1'b0}}), .out(_4_PC_1), .cin(1'b0));  // open: cout

  // Other names for the same wires on the sheet: buff2[25:0] = _2_Out26; buff4_t[20:11] = {_4_rt, _4_rd}

  // Notes on the sheet:
  //   contents of rom_1 (hex, n*v repeats v):
  //   20110001 8000c05 20110001 20120002 20130003 8000c09 20110001 20120002 20130003 8000c0d 20110001
  //   20120002 20130003 8000c11 20110001 20120002 20130003 c000cb8 20100001 20110001 118fc0 112020
  //   20020022 c 118882 12200001 8000c15 112020 20020022 c 20110001 118880 112020 20020022 c 12200001
  //   8000c1f 20110001 118fc0 112020 20020022 c 1188c3 112020 20020022 c 118903 112020 20020022 c 118903
  //   112020 20020022 c 118903 112020 20020022 c 118903 112020 20020022 c 118903 112020 20020022 c 118903
  //   112020 20020022 c 118903 112020 20020022 c 20100001 109fc0 139fc3 8021 2012000c 24160003 26100001
  //   3210000f 20080008 20090001 139900 2709825 132020 20020022 c 1094022 1500fff9 22100001 2018000f
  //   2188024 108700 20080008 20090001 139902 2709825 132021 20020022 c 1094022 1500fff9 108702 2c9b022
  //   12c00001 8000c50 4020 1084027 84400 3508ffff 82021 20020022 c 2010ffff 20110000 ae300000 22100001
  //   22310004 ae300000 22100001 22310004 ae300000 22100001 22310004 ae300000 22100001 22310004 ae300000
  //   22100001 22310004 ae300000 22100001 22310004 ae300000 22100001 22310004 ae300000 22100001 22310004
  //   ae300000 22100001 22310004 ae300000 22100001 22310004 ae300000 22100001 22310004 ae300000 22100001
  //   22310004 ae300000 22100001 22310004 ae300000 22100001 22310004 ae300000 22100001 22310004 ae300000
  //   22100001 22310004 22100001 8020 2011003c 8e130000 8e340000 274402a 11000002 ae330000 ae140000
  //   2231fffc 1611fff8 102020 20020022 c 22100004 2011003c 1611fff2 2002000a c 20100000 22100001 102020
  //   20020022 c 22100002 102020 20020022 c 22100003 102020 20020022 c 22100004 102020 20020022 c 22100005
  //   102020 20020022 c 22100006 102020 20020022 c 22100007 102020 20020022 c 22100008 102020 20020022
  //   20020022 c 3e00008
  //   clk
  //   B_sucess
  //   Jump_beq_bne
  //   Load_Use
  //   JAL
  //   Mem
  //   W#
  //   RE.D1
  //   v0
  //   a0
  //   PC
  //   PC+1
  //   sa
  //   offset
  //   RE.D2
  //   RE.D1
  //   JUMP
  //   RE.D1
  //   AluRes
  //   ALUres
  //   sw
endmodule

module Control (
  input  [31:0] in_1,
  output sw,
  output [1:0] Y_num,
  output rd_only,
  output syscall,
  output R1NoUse,
  output [1:0] R1_num,
  output R2NoUse,
  output R2,
  output [1:0] W_num,
  output [1:0] Din_num,
  output [3:0] OP,
  output [1:0] JumpOp,
  output beq_bne,
  output [4:0] rs_base,
  output [4:0] rt,
  output [4:0] rd,
  output [4:0] sa,
  output [15:0] IMM_offset,
  output [25:0] Out26
);

  wire specialchoice_1_j;
  wire [5:0] specialchoice_1_out;

  SpecialChoice specialchoice_1 (.Hi6(in_1[31:26]), .Lo6(in_1[5:0]), .J(specialchoice_1_j), .Out(specialchoice_1_out));
  Y_Choice y_choice_1 (
    .j(specialchoice_1_j), .a(specialchoice_1_out[5]), .b(specialchoice_1_out[4]),
    .c(specialchoice_1_out[3]), .d(specialchoice_1_out[2]), .e(specialchoice_1_out[1]),
    .f(specialchoice_1_out[0]), .o1(Y_num[1]), .o2(Y_num[0]));
  R1_Mux r1_mux_1 (
    .j(specialchoice_1_j), .a(specialchoice_1_out[5]), .b(specialchoice_1_out[4]), .o(R1_num[0]),
    .c(specialchoice_1_out[3]), .d(specialchoice_1_out[2]), .e(specialchoice_1_out[1]),
    .f(specialchoice_1_out[0]), .o_v0(R1_num[1]));
  R2 r2_1 (
    .j(specialchoice_1_j), .a(specialchoice_1_out[5]), .b(specialchoice_1_out[4]),
    .c(specialchoice_1_out[3]), .d(specialchoice_1_out[2]), .e(specialchoice_1_out[1]),
    .f(specialchoice_1_out[0]), .o1(R2));
  W_Mux w_mux_1 (
    .j(specialchoice_1_j), .a(specialchoice_1_out[5]), .b(specialchoice_1_out[4]),
    .c(specialchoice_1_out[3]), .o1(W_num[0]), .d(specialchoice_1_out[2]), .e(specialchoice_1_out[1]),
    .f(specialchoice_1_out[0]), .o2(W_num[1]));
  Din_Mux din_mux_1 (
    .j(specialchoice_1_j), .a(specialchoice_1_out[5]), .o1(Din_num[0]), .b(specialchoice_1_out[4]),
    .c(specialchoice_1_out[3]), .d(specialchoice_1_out[2]), .o2_H(Din_num[1]), .e(specialchoice_1_out[1]),
    .f(specialchoice_1_out[0]));
  OPchoice opchoice_1 (
    .j(specialchoice_1_j), .a(specialchoice_1_out[5]), .b(specialchoice_1_out[4]),
    .c(specialchoice_1_out[3]), .d(specialchoice_1_out[2]), .e(specialchoice_1_out[1]),
    .f(specialchoice_1_out[0]), .o1(OP[3]), .o2(OP[2]), .o3(OP[1]), .o4(OP[0]));
  JUMP jump_1 (
    .j(specialchoice_1_j), .a(specialchoice_1_out[5]), .b(specialchoice_1_out[4]),
    .c(specialchoice_1_out[3]), .d(specialchoice_1_out[2]), .op1(JumpOp[0]), .e(specialchoice_1_out[1]),
    .f(specialchoice_1_out[0]), .op2(JumpOp[1]), .beq_bne(beq_bne));
  Signal signal_1 (
    .j(specialchoice_1_j), .a(specialchoice_1_out[5]), .sw(sw), .b(specialchoice_1_out[4]),
    .c(specialchoice_1_out[3]), .d(specialchoice_1_out[2]), .e(specialchoice_1_out[1]),
    .f(specialchoice_1_out[0]), .rd_reg(rd_only), .syscall(syscall), .R1NoUse(R1NoUse), .R2NoUse(R2NoUse));

  assign IMM_offset = in_1[15:0];
  assign Out26 = in_1[25:0];
  assign rd = in_1[15:11];
  assign rs_base = in_1[25:21];
  assign rt = in_1[20:16];
  assign sa = in_1[10:6];
endmodule

module R1_Mux (
  input  j,
  input  a,
  input  b,
  input  c,
  input  d,
  input  e,
  input  f,
  output o,
  output o_v0
);

  wire and_1_out, and_2_out, not_1_out, not_2_out, not_3_out, not_4_out, not_5_out, not_6_out, not_7_out,
       not_8_out, not_9_out, not_10_out, not_11_out, not_12_out, not_13_out;

  not not_1 (not_1_out, a);
  not not_2 (not_2_out, b);
  not not_3 (not_3_out, c);
  not not_4 (not_4_out, d);
  not not_5 (not_5_out, f);
  not not_6 (not_6_out, a);
  not not_7 (not_7_out, b);
  not not_8 (not_8_out, c);
  not not_9 (not_9_out, d);
  not not_10 (not_10_out, a);
  not not_11 (not_11_out, b);
  not not_12 (not_12_out, e);
  not not_13 (not_13_out, f);
  and and_1 (and_1_out, j, not_1_out, not_2_out, not_3_out, not_4_out, not_5_out);
  and and_2 (and_2_out, j, not_6_out, not_7_out, not_8_out, not_9_out, e);
  and and_3 (o_v0, j, not_10_out, not_11_out, c, d, not_12_out, not_13_out);
  or or_1 (o, and_1_out, and_2_out);
endmodule

module SpecialChoice (
  input  [5:0] Hi6,
  input  [5:0] Lo6,
  output J,
  output [5:0] Out
);

  wire not_2_out, not_3_out, not_4_out, not_5_out, not_6_out, not_7_out;
  wire [5:0] and_1_out, and_2_out, bit_extender_1_out, not_1_out;

  assign not_1_out = ~bit_extender_1_out;  // NOT_Gate not_1, 6 bits wide
  assign and_1_out = not_1_out & Hi6;  // AND_Gate and_1, 6 bits wide
  assign and_2_out = bit_extender_1_out & Lo6;  // AND_Gate and_2, 6 bits wide
  not not_2 (not_2_out, Hi6[0]);
  not not_3 (not_3_out, Hi6[1]);
  not not_4 (not_4_out, Hi6[2]);
  not not_5 (not_5_out, Hi6[3]);
  not not_6 (not_6_out, Hi6[4]);
  not not_7 (not_7_out, Hi6[5]);
  and and_3 (J, not_2_out, not_3_out, not_4_out, not_5_out, not_6_out, not_7_out);
  assign Out = and_1_out | and_2_out;  // OR_Gate or_1, 6 bits wide
  assign bit_extender_1_out = {{5{J}}, J};  // Bit_Extender bit_extender_1
endmodule

module W_Mux (
  input  j,
  input  a,
  input  b,
  input  c,
  input  d,
  input  e,
  input  f,
  output o1,
  output o2
);

  wire and_1_out, and_2_out, and_3_out, not_1_out, not_2_out, not_3_out, not_4_out, not_5_out, not_6_out,
       not_7_out, not_8_out, not_9_out, not_10_out, not_11_out, not_12_out, not_13_out, not_14_out,
       not_15_out, not_16_out, not_17_out, not_18_out;

  not not_1 (not_1_out, j);
  not not_2 (not_2_out, a);
  not not_3 (not_3_out, b);
  not not_4 (not_4_out, d);
  not not_5 (not_5_out, f);
  not not_6 (not_6_out, j);
  not not_7 (not_7_out, a);
  not not_8 (not_8_out, b);
  not not_9 (not_9_out, e);
  not not_10 (not_10_out, j);
  not not_11 (not_11_out, b);
  not not_12 (not_12_out, c);
  not not_13 (not_13_out, d);
  not not_14 (not_14_out, j);
  not not_15 (not_15_out, a);
  not not_16 (not_16_out, b);
  not not_17 (not_17_out, c);
  not not_18 (not_18_out, d);
  and and_1 (and_1_out, not_1_out, not_2_out, not_3_out, c, not_4_out, not_5_out);
  and and_2 (and_2_out, not_6_out, not_7_out, not_8_out, c, not_9_out);
  and and_3 (and_3_out, not_10_out, a, not_11_out, not_12_out, not_13_out, e, f);
  and and_4 (o2, not_14_out, not_15_out, not_16_out, not_17_out, not_18_out, e, f);
  or or_1 (o1, and_1_out, and_2_out, and_3_out);
endmodule

module Din_Mux (
  input  j,
  input  a,
  input  b,
  input  c,
  input  d,
  input  e,
  input  f,
  output o1,
  output o2_H
);

  wire not_1_out, not_2_out, not_3_out, not_4_out, not_5_out, not_6_out, not_7_out, not_8_out, not_9_out;

  not not_1 (not_1_out, j);
  not not_2 (not_2_out, b);
  not not_3 (not_3_out, c);
  not not_4 (not_4_out, d);
  not not_5 (not_5_out, j);
  not not_6 (not_6_out, a);
  not not_7 (not_7_out, b);
  not not_8 (not_8_out, c);
  not not_9 (not_9_out, d);
  and and_1 (o1, not_1_out, a, not_2_out, not_3_out, not_4_out, e, f);
  and and_2 (o2_H, not_5_out, not_6_out, not_7_out, not_8_out, not_9_out, e, f);
endmodule

module Y_Choice (
  input  j,
  input  a,
  input  b,
  input  c,
  input  d,
  input  e,
  input  f,
  output o1,
  output o2
);

  wire and_1_out, and_2_out, and_3_out, and_4_out, and_5_out, and_6_out, and_7_out, and_8_out, not_1_out,
       not_2_out, not_3_out, not_4_out, not_5_out, not_6_out, not_7_out, not_8_out, not_9_out, not_10_out,
       not_11_out, not_12_out, not_13_out, not_14_out, not_15_out, not_16_out, not_17_out, not_18_out,
       not_19_out, not_20_out, not_21_out, not_22_out, not_23_out, not_24_out, not_25_out, not_26_out,
       not_27_out, not_28_out, not_29_out, not_30_out, not_31_out, not_32_out, not_33_out, not_34_out,
       not_35_out;

  not not_1 (not_1_out, j);
  not not_2 (not_2_out, a);
  not not_3 (not_3_out, b);
  not not_4 (not_4_out, e);
  not not_5 (not_5_out, a);
  not not_6 (not_6_out, b);
  not not_7 (not_7_out, c);
  not not_8 (not_8_out, d);
  not not_9 (not_9_out, f);
  not not_10 (not_10_out, a);
  not not_11 (not_11_out, b);
  not not_12 (not_12_out, c);
  not not_13 (not_13_out, d);
  not not_14 (not_14_out, j);
  not not_15 (not_15_out, a);
  not not_16 (not_16_out, b);
  not not_17 (not_17_out, d);
  not not_18 (not_18_out, e);
  not not_19 (not_19_out, j);
  not not_20 (not_20_out, a);
  not not_21 (not_21_out, b);
  not not_22 (not_22_out, d);
  not not_23 (not_23_out, f);
  not not_24 (not_24_out, j);
  not not_25 (not_25_out, b);
  not not_26 (not_26_out, d);
  not not_27 (not_27_out, a);
  not not_28 (not_28_out, b);
  not not_29 (not_29_out, c);
  not not_30 (not_30_out, d);
  not not_31 (not_31_out, f);
  not not_32 (not_32_out, a);
  not not_33 (not_33_out, b);
  not not_34 (not_34_out, c);
  not not_35 (not_35_out, d);
  and and_1 (and_1_out, not_1_out, not_2_out, not_3_out, c, d, not_4_out);
  and and_2 (and_2_out, j, not_5_out, not_6_out, not_7_out, not_8_out, not_9_out);
  and and_3 (and_3_out, j, not_10_out, not_11_out, not_12_out, not_13_out, e);
  and and_4 (and_4_out, not_14_out, not_15_out, not_16_out, c, not_17_out, not_18_out);
  and and_5 (and_5_out, not_19_out, not_20_out, not_21_out, c, not_22_out, not_23_out);
  and and_6 (and_6_out, not_24_out, a, not_25_out, not_26_out, e, f);
  and and_7 (and_7_out, j, not_27_out, not_28_out, not_29_out, not_30_out, not_31_out);
  and and_8 (and_8_out, j, not_32_out, not_33_out, not_34_out, not_35_out, e);
  or or_1 (o1, and_1_out, and_2_out, and_3_out);
  or or_2 (o2, and_4_out, and_5_out, and_6_out, and_7_out, and_8_out);

  // Notes on the sheet:
  //   o1 o2
  //   RE.D2 00 
  //   S   01
  //   Z   10
  //   sa   11
endmodule

module OPchoice (
  input  j,
  input  a,
  input  b,
  input  c,
  input  d,
  input  e,
  input  f,
  output o1,
  output o2,
  output o3,
  output o4
);

  wire and_1_out, and_2_out, and_3_out, and_4_out, and_5_out, and_6_out, and_7_out, and_8_out, and_9_out,
       and_10_out, and_11_out, and_12_out, and_13_out, and_14_out, and_15_out, and_16_out, and_17_out,
       and_18_out, and_19_out, and_20_out, and_21_out, and_22_out, and_23_out, and_24_out, and_25_out,
       and_26_out, and_27_out, and_28_out, and_29_out, and_30_out, and_31_out, and_32_out, and_33_out,
       and_34_out, not_1_out, not_2_out, not_3_out, not_4_out, not_5_out, not_6_out, not_7_out, not_8_out,
       not_9_out, not_10_out, not_11_out, not_12_out, not_13_out, not_14_out, not_15_out, not_16_out,
       not_17_out, not_18_out, not_19_out, not_20_out, not_21_out, not_22_out, not_23_out, not_24_out,
       not_25_out, not_26_out, not_27_out, not_28_out, not_29_out, not_30_out, not_31_out, not_32_out,
       not_33_out, not_34_out, not_35_out, not_36_out, not_37_out, not_38_out, not_39_out, not_40_out,
       not_41_out, not_42_out, not_43_out, not_44_out, not_45_out, not_46_out, not_47_out, not_48_out,
       not_49_out, not_50_out, not_51_out, not_52_out, not_53_out, not_54_out, not_55_out, not_56_out,
       not_57_out, not_58_out, not_59_out, not_60_out, not_61_out, not_62_out, not_63_out, not_64_out,
       not_65_out, not_66_out, not_67_out, not_68_out, not_69_out, not_70_out, not_71_out, not_72_out,
       not_73_out, not_74_out, not_75_out, not_76_out, not_77_out, not_78_out, not_79_out, not_80_out,
       not_81_out, not_82_out, not_83_out, not_84_out, not_85_out, not_86_out, not_87_out, not_88_out,
       not_89_out, not_90_out, not_91_out, not_92_out, not_93_out, not_94_out, not_95_out, not_96_out,
       not_97_out, not_98_out, not_99_out, not_100_out, not_101_out, not_102_out, not_103_out, not_104_out,
       not_105_out, not_106_out, not_107_out, not_108_out, not_109_out, not_110_out, not_111_out,
       not_112_out, not_113_out, not_114_out, not_115_out, not_116_out, not_117_out, not_118_out,
       not_119_out, not_120_out, not_121_out, not_122_out, not_123_out, not_124_out, not_125_out,
       not_126_out, not_127_out, not_128_out, not_129_out, not_130_out, not_131_out, not_132_out,
       not_133_out, not_134_out, not_135_out, not_136_out, not_137_out;

  not not_1 (not_1_out, b);
  not not_2 (not_2_out, c);
  not not_3 (not_3_out, e);
  not not_4 (not_4_out, j);
  not not_5 (not_5_out, a);
  not not_6 (not_6_out, b);
  not not_7 (not_7_out, e);
  not not_8 (not_8_out, b);
  not not_9 (not_9_out, c);
  not not_10 (not_10_out, b);
  not not_11 (not_11_out, d);
  not not_12 (not_12_out, f);
  not not_13 (not_13_out, j);
  not not_14 (not_14_out, a);
  not not_15 (not_15_out, b);
  not not_16 (not_16_out, d);
  not not_17 (not_17_out, f);
  not not_18 (not_18_out, b);
  not not_19 (not_19_out, d);
  not not_20 (not_20_out, b);
  not not_21 (not_21_out, c);
  not not_22 (not_22_out, d);
  not not_23 (not_23_out, e);
  not not_24 (not_24_out, f);
  not not_25 (not_25_out, j);
  not not_26 (not_26_out, a);
  not not_27 (not_27_out, b);
  not not_28 (not_28_out, d);
  not not_29 (not_29_out, e);
  not not_30 (not_30_out, f);
  not not_31 (not_31_out, j);
  not not_32 (not_32_out, a);
  not not_33 (not_33_out, b);
  not not_34 (not_34_out, d);
  not not_35 (not_35_out, e);
  not not_36 (not_36_out, b);
  not not_37 (not_37_out, c);
  not not_38 (not_38_out, d);
  not not_39 (not_39_out, e);
  not not_40 (not_40_out, b);
  not not_41 (not_41_out, c);
  not not_42 (not_42_out, e);
  not not_43 (not_43_out, f);
  not not_44 (not_44_out, j);
  not not_45 (not_45_out, a);
  not not_46 (not_46_out, b);
  not not_47 (not_47_out, e);
  not not_48 (not_48_out, f);
  not not_49 (not_49_out, b);
  not not_50 (not_50_out, c);
  not not_51 (not_51_out, d);
  not not_52 (not_52_out, f);
  not not_53 (not_53_out, j);
  not not_54 (not_54_out, b);
  not not_55 (not_55_out, c);
  not not_56 (not_56_out, d);
  not not_57 (not_57_out, j);
  not not_58 (not_58_out, b);
  not not_59 (not_59_out, d);
  not not_60 (not_60_out, b);
  not not_61 (not_61_out, d);
  not not_62 (not_62_out, b);
  not not_63 (not_63_out, c);
  not not_64 (not_64_out, e);
  not not_65 (not_65_out, f);
  not not_66 (not_66_out, j);
  not not_67 (not_67_out, a);
  not not_68 (not_68_out, b);
  not not_69 (not_69_out, e);
  not not_70 (not_70_out, f);
  not not_71 (not_71_out, a);
  not not_72 (not_72_out, b);
  not not_73 (not_73_out, c);
  not not_74 (not_74_out, d);
  not not_75 (not_75_out, b);
  not not_76 (not_76_out, c);
  not not_77 (not_77_out, d);
  not not_78 (not_78_out, f);
  not not_79 (not_79_out, b);
  not not_80 (not_80_out, c);
  not not_81 (not_81_out, b);
  not not_82 (not_82_out, d);
  not not_83 (not_83_out, f);
  not not_84 (not_84_out, j);
  not not_85 (not_85_out, a);
  not not_86 (not_86_out, b);
  not not_87 (not_87_out, d);
  not not_88 (not_88_out, f);
  not not_89 (not_89_out, b);
  not not_90 (not_90_out, c);
  not not_91 (not_91_out, d);
  not not_92 (not_92_out, e);
  not not_93 (not_93_out, f);
  not not_94 (not_94_out, j);
  not not_95 (not_95_out, a);
  not not_96 (not_96_out, b);
  not not_97 (not_97_out, d);
  not not_98 (not_98_out, e);
  not not_99 (not_99_out, f);
  not not_100 (not_100_out, j);
  not not_101 (not_101_out, a);
  not not_102 (not_102_out, b);
  not not_103 (not_103_out, d);
  not not_104 (not_104_out, e);
  not not_105 (not_105_out, b);
  not not_106 (not_106_out, c);
  not not_107 (not_107_out, d);
  not not_108 (not_108_out, e);
  not not_109 (not_109_out, b);
  not not_110 (not_110_out, c);
  not not_111 (not_111_out, e);
  not not_112 (not_112_out, f);
  not not_113 (not_113_out, j);
  not not_114 (not_114_out, a);
  not not_115 (not_115_out, b);
  not not_116 (not_116_out, e);
  not not_117 (not_117_out, f);
  not not_118 (not_118_out, a);
  not not_119 (not_119_out, b);
  not not_120 (not_120_out, c);
  not not_121 (not_121_out, d);
  not not_122 (not_122_out, f);
  not not_123 (not_123_out, j);
  not not_124 (not_124_out, b);
  not not_125 (not_125_out, c);
  not not_126 (not_126_out, d);
  not not_127 (not_127_out, j);
  not not_128 (not_128_out, b);
  not not_129 (not_129_out, d);
  not not_130 (not_130_out, b);
  not not_131 (not_131_out, d);
  not not_132 (not_132_out, f);
  not not_133 (not_133_out, j);
  not not_134 (not_134_out, a);
  not not_135 (not_135_out, b);
  not not_136 (not_136_out, d);
  not not_137 (not_137_out, f);
  and and_1 (and_1_out, j, a, not_1_out, not_2_out, d, not_3_out, f);
  and and_2 (and_2_out, not_4_out, not_5_out, not_6_out, c, d, not_7_out, f);
  and and_3 (and_3_out, j, a, not_8_out, not_9_out, d, e, f);
  and and_4 (and_4_out, j, a, not_10_out, c, not_11_out, e, not_12_out);
  and and_5 (and_5_out, not_13_out, not_14_out, not_15_out, c, not_16_out, e, not_17_out);
  and and_6 (and_6_out, j, a, not_18_out, c, not_19_out, e, f);
  and and_7 (and_7_out, j, a, not_20_out, not_21_out, not_22_out, not_23_out, not_24_out);
  and and_8 (and_8_out, not_25_out, not_26_out, not_27_out, c, not_28_out, not_29_out, not_30_out);
  and and_9 (and_9_out, not_31_out, not_32_out, not_33_out, c, not_34_out, not_35_out, f);
  and and_10 (and_10_out, j, a, not_36_out, not_37_out, not_38_out, not_39_out, f);
  and and_11 (and_11_out, j, a, not_40_out, not_41_out, d, not_42_out, not_43_out);
  and and_12 (and_12_out, not_44_out, not_45_out, not_46_out, c, d, not_47_out, not_48_out);
  and and_13 (and_13_out, j, a, not_49_out, not_50_out, not_51_out, e, not_52_out);
  and and_14 (and_14_out, not_53_out, a, not_54_out, not_55_out, not_56_out, e, f);
  and and_15 (and_15_out, not_57_out, a, not_58_out, c, not_59_out, e, f);
  and and_16 (and_16_out, j, a, not_60_out, c, not_61_out, e, f);
  and and_17 (and_17_out, j, a, not_62_out, not_63_out, d, not_64_out, not_65_out);
  and and_18 (and_18_out, not_66_out, not_67_out, not_68_out, c, d, not_69_out, not_70_out);
  and and_19 (and_19_out, j, not_71_out, not_72_out, not_73_out, not_74_out, e, f);
  and and_20 (and_20_out, j, a, not_75_out, not_76_out, not_77_out, e, not_78_out);
  and and_21 (and_21_out, j, a, not_79_out, not_80_out, d, e, f);
  and and_22 (and_22_out, j, a, not_81_out, c, not_82_out, e, not_83_out);
  and and_23 (and_23_out, not_84_out, not_85_out, not_86_out, c, not_87_out, e, not_88_out);
  and and_24 (and_24_out, j, a, not_89_out, not_90_out, not_91_out, not_92_out, not_93_out);
  and and_25 (and_25_out, not_94_out, not_95_out, not_96_out, c, not_97_out, not_98_out, not_99_out);
  and and_26 (and_26_out, not_100_out, not_101_out, not_102_out, c, not_103_out, not_104_out, f);
  and and_27 (and_27_out, j, a, not_105_out, not_106_out, not_107_out, not_108_out, f);
  and and_28 (and_28_out, j, a, not_109_out, not_110_out, d, not_111_out, not_112_out);
  and and_29 (and_29_out, not_113_out, not_114_out, not_115_out, c, d, not_116_out, not_117_out);
  and and_30 (and_30_out, j, not_118_out, not_119_out, not_120_out, not_121_out, e, not_122_out);
  and and_31 (and_31_out, not_123_out, a, not_124_out, not_125_out, not_126_out, e, f);
  and and_32 (and_32_out, not_127_out, a, not_128_out, c, not_129_out, e, f);
  and and_33 (and_33_out, j, a, not_130_out, c, not_131_out, e, not_132_out);
  and and_34 (and_34_out, not_133_out, not_134_out, not_135_out, c, not_136_out, e, not_137_out);
  or or_1 (o1, and_1_out, and_2_out, and_3_out, and_4_out, and_5_out, and_6_out);
  or or_2 (o2, and_7_out, and_8_out, and_9_out, and_10_out, and_11_out, and_12_out, and_13_out, and_14_out, and_15_out, and_16_out);
  or or_3 (o3, and_17_out, and_18_out, and_19_out, and_20_out, and_21_out, and_22_out, and_23_out);
  or or_4 (o4, and_24_out, and_25_out, and_26_out, and_27_out, and_28_out, and_29_out, and_30_out, and_31_out, and_32_out, and_33_out, and_34_out);
endmodule

module JUMP (
  input  j,
  input  a,
  input  b,
  input  c,
  input  d,
  input  e,
  input  f,
  output op1,
  output op2,
  output beq_bne
);

  wire and_1_out, and_2_out, and_3_out, and_4_out, and_5_out, and_6_out, and_7_out, not_1_out, not_2_out,
       not_3_out, not_4_out, not_5_out, not_6_out, not_7_out, not_8_out, not_9_out, not_10_out, not_11_out,
       not_12_out, not_13_out, not_14_out, not_15_out, not_16_out, not_17_out, not_18_out, not_19_out,
       not_20_out, not_21_out, not_22_out, not_23_out, not_24_out, not_25_out, not_26_out, not_27_out,
       not_28_out, not_29_out, not_30_out, not_31_out, not_32_out, not_33_out, not_34_out, not_35_out,
       not_36_out, not_37_out, not_38_out, not_39_out, not_40_out, not_41_out, not_42_out, not_43_out,
       not_44_out;

  not not_1 (not_1_out, a);
  not not_2 (not_2_out, b);
  not not_3 (not_3_out, d);
  not not_4 (not_4_out, e);
  not not_5 (not_5_out, f);
  not not_6 (not_6_out, j);
  not not_7 (not_7_out, a);
  not not_8 (not_8_out, b);
  not not_9 (not_9_out, c);
  not not_10 (not_10_out, e);
  not not_11 (not_11_out, f);
  not not_12 (not_12_out, j);
  not not_13 (not_13_out, a);
  not not_14 (not_14_out, b);
  not not_15 (not_15_out, c);
  not not_16 (not_16_out, e);
  not not_17 (not_17_out, j);
  not not_18 (not_18_out, a);
  not not_19 (not_19_out, b);
  not not_20 (not_20_out, c);
  not not_21 (not_21_out, d);
  not not_22 (not_22_out, f);
  not not_23 (not_23_out, j);
  not not_24 (not_24_out, a);
  not not_25 (not_25_out, b);
  not not_26 (not_26_out, c);
  not not_27 (not_27_out, d);
  not not_28 (not_28_out, j);
  not not_29 (not_29_out, a);
  not not_30 (not_30_out, b);
  not not_31 (not_31_out, c);
  not not_32 (not_32_out, e);
  not not_33 (not_33_out, f);
  not not_34 (not_34_out, j);
  not not_35 (not_35_out, a);
  not not_36 (not_36_out, b);
  not not_37 (not_37_out, c);
  not not_38 (not_38_out, e);
  not not_39 (not_39_out, j);
  not not_40 (not_40_out, a);
  not not_41 (not_41_out, b);
  not not_42 (not_42_out, c);
  not not_43 (not_43_out, e);
  not not_44 (not_44_out, f);
  and and_1 (and_1_out, j, not_1_out, not_2_out, c, not_3_out, not_4_out, not_5_out);
  and and_2 (and_2_out, not_6_out, not_7_out, not_8_out, not_9_out, d, not_10_out, not_11_out);
  and and_3 (and_3_out, not_12_out, not_13_out, not_14_out, not_15_out, d, not_16_out, f);
  and and_4 (and_4_out, not_17_out, not_18_out, not_19_out, not_20_out, not_21_out, e, not_22_out);
  and and_5 (and_5_out, not_23_out, not_24_out, not_25_out, not_26_out, not_27_out, e, f);
  and and_6 (and_6_out, not_28_out, not_29_out, not_30_out, not_31_out, d, not_32_out, not_33_out);
  and and_7 (and_7_out, not_34_out, not_35_out, not_36_out, not_37_out, d, not_38_out, f);
  and and_8 (beq_bne, not_39_out, not_40_out, not_41_out, not_42_out, d, not_43_out, not_44_out);
  or or_1 (op1, and_1_out, and_2_out, and_3_out);
  or or_2 (op2, and_4_out, and_5_out, and_6_out, and_7_out);
endmodule

module R2 (
  input  j,
  input  a,
  input  b,
  input  c,
  input  d,
  input  e,
  input  f,
  output o1
);

  wire not_1_out, not_2_out, not_3_out, not_4_out;

  not not_1 (not_1_out, a);
  not not_2 (not_2_out, b);
  not not_3 (not_3_out, e);
  not not_4 (not_4_out, f);
  and and_1 (o1, j, not_1_out, not_2_out, c, d, not_3_out, not_4_out);
endmodule

module Signal (
  input  j,
  input  a,
  input  b,
  input  c,
  input  d,
  input  e,
  input  f,
  output sw,
  output rd_reg,
  output syscall,
  output R1NoUse,
  output R2NoUse
);

  wire and_2_out, and_3_out, and_4_out, and_5_out, and_6_out, and_7_out, and_8_out, and_9_out, and_11_out,
       and_12_out, and_13_out, and_14_out, and_15_out, and_16_out, and_17_out, and_18_out, and_19_out,
       and_20_out, and_21_out, and_22_out, and_23_out, and_24_out, not_1_out, not_2_out, not_3_out,
       not_4_out, not_5_out, not_6_out, not_7_out, not_8_out, not_9_out, not_10_out, not_11_out, not_12_out,
       not_13_out, not_14_out, not_15_out, not_16_out, not_17_out, not_18_out, not_19_out, not_20_out,
       not_21_out, not_22_out, not_23_out, not_24_out, not_25_out, not_26_out, not_27_out, not_28_out,
       not_29_out, not_30_out, not_31_out, not_32_out, not_33_out, not_34_out, not_35_out, not_36_out,
       not_37_out, not_38_out, not_39_out, not_40_out, not_41_out, not_42_out, not_43_out, not_44_out,
       not_45_out, not_46_out, not_47_out, not_48_out, not_49_out, not_50_out, not_51_out, not_52_out,
       not_53_out, not_54_out, not_55_out, not_56_out, not_57_out, not_58_out, not_59_out, not_60_out,
       not_61_out, not_62_out, not_63_out, not_64_out, not_65_out, not_66_out, not_67_out, not_68_out,
       not_69_out, not_70_out, not_71_out, not_72_out, not_73_out, not_74_out, not_75_out, not_76_out,
       not_77_out, not_78_out, not_79_out, not_80_out, not_81_out, not_82_out, not_83_out, not_84_out,
       not_85_out, not_86_out, not_87_out, not_88_out, not_89_out, not_90_out, not_91_out, not_92_out,
       not_93_out, not_94_out, not_95_out, not_96_out, not_97_out, not_98_out, not_99_out, not_100_out,
       not_101_out, not_102_out, not_103_out, not_104_out, not_105_out, not_106_out, not_107_out,
       not_108_out, not_109_out, not_110_out, not_111_out, not_112_out, not_113_out, not_114_out,
       not_115_out, not_116_out, not_117_out, not_118_out, not_119_out;

  not not_1 (not_1_out, j);
  not not_2 (not_2_out, b);
  not not_3 (not_3_out, d);
  not not_4 (not_4_out, j);
  not not_5 (not_5_out, b);
  not not_6 (not_6_out, d);
  not not_7 (not_7_out, j);
  not not_8 (not_8_out, a);
  not not_9 (not_9_out, b);
  not not_10 (not_10_out, c);
  not not_11 (not_11_out, e);
  not not_12 (not_12_out, f);
  not not_13 (not_13_out, j);
  not not_14 (not_14_out, a);
  not not_15 (not_15_out, b);
  not not_16 (not_16_out, c);
  not not_17 (not_17_out, e);
  not not_18 (not_18_out, j);
  not not_19 (not_19_out, a);
  not not_20 (not_20_out, b);
  not not_21 (not_21_out, c);
  not not_22 (not_22_out, d);
  not not_23 (not_23_out, f);
  not not_24 (not_24_out, a);
  not not_25 (not_25_out, b);
  not not_26 (not_26_out, d);
  not not_27 (not_27_out, e);
  not not_28 (not_28_out, f);
  not not_29 (not_29_out, a);
  not not_30 (not_30_out, b);
  not not_31 (not_31_out, e);
  not not_32 (not_32_out, f);
  not not_33 (not_33_out, j);
  not not_34 (not_34_out, a);
  not not_35 (not_35_out, c);
  not not_36 (not_36_out, d);
  not not_37 (not_37_out, e);
  not not_38 (not_38_out, f);
  not not_39 (not_39_out, j);
  not not_40 (not_40_out, a);
  not not_41 (not_41_out, c);
  not not_42 (not_42_out, d);
  not not_43 (not_43_out, e);
  not not_44 (not_44_out, f);
  not not_45 (not_45_out, a);
  not not_46 (not_46_out, b);
  not not_47 (not_47_out, e);
  not not_48 (not_48_out, f);
  not not_49 (not_49_out, j);
  not not_50 (not_50_out, a);
  not not_51 (not_51_out, b);
  not not_52 (not_52_out, c);
  not not_53 (not_53_out, d);
  not not_54 (not_54_out, f);
  not not_55 (not_55_out, j);
  not not_56 (not_56_out, a);
  not not_57 (not_57_out, b);
  not not_58 (not_58_out, c);
  not not_59 (not_59_out, d);
  not not_60 (not_60_out, j);
  not not_61 (not_61_out, a);
  not not_62 (not_62_out, b);
  not not_63 (not_63_out, d);
  not not_64 (not_64_out, e);
  not not_65 (not_65_out, f);
  not not_66 (not_66_out, j);
  not not_67 (not_67_out, a);
  not not_68 (not_68_out, b);
  not not_69 (not_69_out, d);
  not not_70 (not_70_out, e);
  not not_71 (not_71_out, j);
  not not_72 (not_72_out, a);
  not not_73 (not_73_out, b);
  not not_74 (not_74_out, e);
  not not_75 (not_75_out, f);
  not not_76 (not_76_out, a);
  not not_77 (not_77_out, b);
  not not_78 (not_78_out, c);
  not not_79 (not_79_out, d);
  not not_80 (not_80_out, e);
  not not_81 (not_81_out, f);
  not not_82 (not_82_out, a);
  not not_83 (not_83_out, b);
  not not_84 (not_84_out, c);
  not not_85 (not_85_out, d);
  not not_86 (not_86_out, a);
  not not_87 (not_87_out, b);
  not not_88 (not_88_out, c);
  not not_89 (not_89_out, d);
  not not_90 (not_90_out, f);
  not not_91 (not_91_out, j);
  not not_92 (not_92_out, a);
  not not_93 (not_93_out, b);
  not not_94 (not_94_out, e);
  not not_95 (not_95_out, j);
  not not_96 (not_96_out, b);
  not not_97 (not_97_out, c);
  not not_98 (not_98_out, d);
  not not_99 (not_99_out, j);
  not not_100 (not_100_out, a);
  not not_101 (not_101_out, b);
  not not_102 (not_102_out, d);
  not not_103 (not_103_out, f);
  not not_104 (not_104_out, j);
  not not_105 (not_105_out, a);
  not not_106 (not_106_out, b);
  not not_107 (not_107_out, c);
  not not_108 (not_108_out, d);
  not not_109 (not_109_out, f);
  not not_110 (not_110_out, j);
  not not_111 (not_111_out, a);
  not not_112 (not_112_out, b);
  not not_113 (not_113_out, c);
  not not_114 (not_114_out, d);
  not not_115 (not_115_out, a);
  not not_116 (not_116_out, b);
  not not_117 (not_117_out, d);
  not not_118 (not_118_out, e);
  not not_119 (not_119_out, f);
  and and_1 (sw, not_1_out, a, not_2_out, c, not_3_out, e, f);
  and and_2 (and_2_out, not_4_out, a, not_5_out, c, not_6_out, e, f);
  and and_3 (and_3_out, not_7_out, not_8_out, not_9_out, not_10_out, d, not_11_out, not_12_out);
  and and_4 (and_4_out, not_13_out, not_14_out, not_15_out, not_16_out, d, not_17_out, f);
  and and_5 (and_5_out, not_18_out, not_19_out, not_20_out, not_21_out, not_22_out, e, not_23_out);
  and and_6 (and_6_out, j, not_24_out, not_25_out, c, not_26_out, not_27_out, not_28_out);
  and and_7 (and_7_out, j, not_29_out, not_30_out, c, d, not_31_out, not_32_out);
  and and_8 (and_8_out, not_33_out, not_34_out, b, not_35_out, not_36_out, not_37_out, not_38_out);
  and and_9 (and_9_out, not_39_out, not_40_out, b, not_41_out, not_42_out, not_43_out, not_44_out);
  and and_10 (syscall, j, not_45_out, not_46_out, c, d, not_47_out, not_48_out);
  and and_11 (and_11_out, not_49_out, not_50_out, not_51_out, not_52_out, not_53_out, e, not_54_out);
  and and_12 (and_12_out, not_55_out, not_56_out, not_57_out, not_58_out, not_59_out, e, f);
  and and_13 (and_13_out, not_60_out, not_61_out, not_62_out, c, not_63_out, not_64_out, not_65_out);
  and and_14 (and_14_out, not_66_out, not_67_out, not_68_out, c, not_69_out, not_70_out, f);
  and and_15 (and_15_out, not_71_out, not_72_out, not_73_out, c, d, not_74_out, not_75_out);
  and and_16 (and_16_out, j, not_76_out, not_77_out, not_78_out, not_79_out, not_80_out, not_81_out);
  and and_17 (and_17_out, j, not_82_out, not_83_out, not_84_out, not_85_out, e, f);
  and and_18 (and_18_out, j, not_86_out, not_87_out, not_88_out, not_89_out, e, not_90_out);
  and and_19 (and_19_out, not_91_out, not_92_out, not_93_out, c, d, not_94_out, f);
  and and_20 (and_20_out, not_95_out, a, not_96_out, not_97_out, not_98_out, e, f);
  and and_21 (and_21_out, not_99_out, not_100_out, not_101_out, c, not_102_out, e, not_103_out);
  and and_22 (and_22_out, not_104_out, not_105_out, not_106_out, not_107_out, not_108_out, e, not_109_out);
  and and_23 (and_23_out, not_110_out, not_111_out, not_112_out, not_113_out, not_114_out, e, f);
  and and_24 (and_24_out, j, not_115_out, not_116_out, c, not_117_out, not_118_out, not_119_out);
  or or_1 (R1NoUse, and_11_out, and_12_out);
  or or_2 (rd_reg, and_2_out, and_3_out, and_4_out, and_5_out, and_6_out, and_7_out, and_8_out, and_9_out);
  or or_3 (R2NoUse, and_13_out, and_14_out, and_15_out, and_16_out, and_17_out, and_18_out, and_19_out, and_20_out, and_21_out, and_22_out, and_23_out, and_24_out);
endmodule

module IF_ID (
  input  clk,
  input  Keep,
  input  Set0,
  input  [31:0] PC,
  input  [31:0] Instraction,
  output [31:0] PC_out,
  output [31:0] IR_out
);

  wire [31:0] multiplexer_1_out, multiplexer_2_out;

  Multiplexer #(.width(32), .enable("false")) multiplexer_1 (
    .in0(Instraction), .in1({32{1'b0}}), .out(multiplexer_1_out), .sel(Set0));
  Multiplexer #(.width(32), .enable("false")) multiplexer_2 (
    .in0(PC), .in1({32{1'b0}}), .out(multiplexer_2_out), .sel(Set0));
  Register #(.width(32)) PC_reg (.D(multiplexer_2_out), .en(Keep), .Q(PC_out), .clk(clk), .clr(1'b0));
  Register #(.width(32)) IR (.D(multiplexer_1_out), .en(Keep), .Q(IR_out), .clk(clk), .clr(1'b0));
endmodule

module ID_Ex (
  input  clk,
  input  Set0,
  input  [31:0] PC,
  input  [31:0] Instraction,
  input  [1:0] W_num,
  input  [1:0] Din_num,
  input  rd_only,
  input  [31:0] MemIn,
  input  sw,
  input  [1:0] Y_num,
  input  [3:0] op,
  input  [31:0] RE_D1,
  input  [31:0] RE_D2,
  input  bne_beq,
  input  [1:0] Jump_op,
  input  syscall,
  input  [1:0] X_num,
  input  [1:0] Y_num_2,
  output [31:0] PC_out,
  output [31:0] IR_out,
  output [1:0] W__out,
  output [1:0] Din_out,
  output rd_only_2,
  output [31:0] MemIn_2,
  output sw_2,
  output [1:0] Y__out,
  output [3:0] op__out,
  output [31:0] RE_D1_2,
  output [31:0] RE_D2_2,
  output bne_beq_2,
  output [1:0] Jump_op_2,
  output syscall_2,
  output [1:0] X,
  output [1:0] Y
);

  wire multiplexer_5_out, multiplexer_7_out, multiplexer_12_out, multiplexer_14_out;
  wire [1:0] multiplexer_3_out, multiplexer_4_out, multiplexer_8_out, multiplexer_13_out, multiplexer_15_out,
       multiplexer_16_out;
  wire [3:0] multiplexer_9_out;
  wire [31:0] multiplexer_1_out, multiplexer_2_out, multiplexer_6_out, multiplexer_10_out, multiplexer_11_out;

  Multiplexer #(.width(32), .disabled(0), .enable("false")) multiplexer_1 (
    .in0(PC), .in1({32{1'b0}}), .out(multiplexer_1_out), .sel(Set0));
  Multiplexer #(.width(32), .disabled(0), .enable("false")) multiplexer_2 (
    .in0(Instraction), .in1({32{1'b0}}), .out(multiplexer_2_out), .sel(Set0));
  Multiplexer #(.width(2), .enable("false")) multiplexer_3 (
    .in0(W_num), .in1(2'b00), .out(multiplexer_3_out), .sel(Set0));
  Multiplexer #(.width(2), .enable("false")) multiplexer_4 (
    .in0(Din_num), .in1(2'b00), .out(multiplexer_4_out), .sel(Set0));
  Multiplexer #(.disabled(0), .enable("false")) multiplexer_5 (
    .in0(rd_only), .in1(1'b0), .out(multiplexer_5_out), .sel(Set0));
  Multiplexer #(.width(32), .disabled(0), .enable("false")) multiplexer_6 (
    .in0(MemIn), .in1({32{1'b0}}), .out(multiplexer_6_out), .sel(Set0));
  Multiplexer #(.disabled(0), .enable("false")) multiplexer_7 (
    .in0(sw), .in1(1'b0), .out(multiplexer_7_out), .sel(Set0));
  Multiplexer #(.width(2), .enable("false")) multiplexer_8 (
    .in0(Y_num), .in1(2'b00), .out(multiplexer_8_out), .sel(Set0));
  Multiplexer #(.width(4), .enable("false")) multiplexer_9 (
    .in0(op), .in1(4'b0000), .out(multiplexer_9_out), .sel(Set0));
  Multiplexer #(.width(32), .disabled(0), .enable("false")) multiplexer_10 (
    .in0(RE_D1), .in1({32{1'b0}}), .out(multiplexer_10_out), .sel(Set0));
  Multiplexer #(.width(32), .disabled(0), .enable("false")) multiplexer_11 (
    .in0(RE_D2), .in1({32{1'b0}}), .out(multiplexer_11_out), .sel(Set0));
  Multiplexer #(.disabled(0), .enable("false")) multiplexer_12 (
    .in0(bne_beq), .in1(1'b0), .out(multiplexer_12_out), .sel(Set0));
  Multiplexer #(.width(2), .enable("false")) multiplexer_13 (
    .in0(Jump_op), .in1(2'b00), .out(multiplexer_13_out), .sel(Set0));
  Multiplexer #(.disabled(0), .enable("false")) multiplexer_14 (
    .in0(syscall), .in1(1'b0), .out(multiplexer_14_out), .sel(Set0));
  Multiplexer #(.width(2), .enable("false")) multiplexer_15 (
    .in0(X_num), .in1(2'b00), .out(multiplexer_15_out), .sel(Set0));
  Multiplexer #(.width(2), .disabled(0), .enable("false")) multiplexer_16 (
    .in0(Y_num_2), .in1(2'b00), .out(multiplexer_16_out), .sel(Set0));
  Register #(.width(32)) PC_reg (.D(multiplexer_1_out), .en(1'b1), .Q(PC_out), .clk(clk), .clr(1'b0));
  Register #(.width(32)) IR (.D(multiplexer_2_out), .en(1'b1), .Q(IR_out), .clk(clk), .clr(1'b0));
  Register #(.width(2)) W (.D(multiplexer_3_out), .en(1'b1), .Q(W__out), .clk(clk), .clr(1'b0));
  Register #(.width(2)) Din (.D(multiplexer_4_out), .en(1'b1), .Q(Din_out), .clk(clk), .clr(1'b0));
  Register #(.width(1)) Din_2 (.D(multiplexer_5_out), .en(1'b1), .Q(rd_only_2), .clk(clk), .clr(1'b0));
  Register #(.width(32)) mem (.D(multiplexer_6_out), .en(1'b1), .Q(MemIn_2), .clk(clk), .clr(1'b0));
  Register #(.width(1)) register_1 (.D(multiplexer_7_out), .en(1'b1), .Q(sw_2), .clk(clk), .clr(1'b0));
  Register #(.width(2)) register_2 (.D(multiplexer_8_out), .en(1'b1), .Q(Y__out), .clk(clk), .clr(1'b0));
  Register #(.width(4)) u_op (.D(multiplexer_9_out), .en(1'b1), .Q(op__out), .clk(clk), .clr(1'b0));
  Register #(.width(32)) register_3 (.D(multiplexer_10_out), .en(1'b1), .Q(RE_D1_2), .clk(clk), .clr(1'b0));
  Register #(.width(32)) register_4 (.D(multiplexer_11_out), .en(1'b1), .Q(RE_D2_2), .clk(clk), .clr(1'b0));
  Register #(.width(1)) register_5 (.D(multiplexer_12_out), .en(1'b1), .Q(bne_beq_2), .clk(clk), .clr(1'b0));
  Register #(.width(2)) register_6 (.D(multiplexer_13_out), .en(1'b1), .Q(Jump_op_2), .clk(clk), .clr(1'b0));
  Register #(.width(1)) register_7 (.D(multiplexer_14_out), .en(1'b1), .Q(syscall_2), .clk(clk), .clr(1'b0));
  Register #(.width(2)) register_8 (.D(multiplexer_15_out), .en(1'b1), .Q(X), .clk(clk), .clr(1'b0));
  Register #(.width(2)) register_9 (.D(multiplexer_16_out), .en(1'b1), .Q(Y), .clk(clk), .clr(1'b0));
endmodule

module EX_MEM (
  input  clk,
  input  [31:0] PC,
  input  [31:0] Instraction,
  input  [1:0] W_num,
  input  [1:0] Din_num,
  input  rd_only,
  input  [31:0] ALU,
  input  [31:0] MemIn,
  input  sw,
  input  halt,
  output [31:0] PC_out,
  output [31:0] IR_out,
  output [1:0] W__out,
  output [1:0] Din_out,
  output rd_only_2,
  output [31:0] ALU_out,
  output [31:0] MemIn_2,
  output sw_2,
  output halt_2
);

  Register #(.width(32)) PC_reg (.D(PC), .en(1'b1), .Q(PC_out), .clk(clk), .clr(1'b0));
  Register #(.width(32)) IR (.D(Instraction), .en(1'b1), .Q(IR_out), .clk(clk), .clr(1'b0));
  Register #(.width(2)) W (.D(W_num), .en(1'b1), .Q(W__out), .clk(clk), .clr(1'b0));
  Register #(.width(2)) Din (.D(Din_num), .en(1'b1), .Q(Din_out), .clk(clk), .clr(1'b0));
  Register #(.width(1)) Din_2 (.D(rd_only), .en(1'b1), .Q(rd_only_2), .clk(clk), .clr(1'b0));
  Register #(.width(32)) u_ALu (.D(ALU), .en(1'b1), .Q(ALU_out), .clk(clk), .clr(1'b0));
  Register #(.width(32)) mem (.D(MemIn), .en(1'b1), .Q(MemIn_2), .clk(clk), .clr(1'b0));
  Register #(.width(1)) register_1 (.D(sw), .en(1'b1), .Q(sw_2), .clk(clk), .clr(1'b0));
  Register #(.width(1)) register_2 (.D(halt), .en(1'b1), .Q(halt_2), .clk(clk), .clr(1'b0));
endmodule

module MEM_WB (
  input  clk,
  input  [31:0] PC,
  input  [31:0] Instraction,
  input  [1:0] W_num,
  input  [1:0] Din_num,
  input  rd_only,
  input  [31:0] ALU,
  input  [31:0] MEM,
  input  halt,
  output [31:0] PC_out,
  output [31:0] IR_out,
  output [1:0] W__out,
  output [1:0] Din_out,
  output rd_only_2,
  output [31:0] ALU_out,
  output [31:0] MEM_out,
  output halt_2
);

  Register #(.width(32)) PC_reg (.D(PC), .en(1'b1), .Q(PC_out), .clk(clk), .clr(1'b0));
  Register #(.width(32)) IR (.D(Instraction), .en(1'b1), .Q(IR_out), .clk(clk), .clr(1'b0));
  Register #(.width(2)) W (.D(W_num), .en(1'b1), .Q(W__out), .clk(clk), .clr(1'b0));
  Register #(.width(2)) Din (.D(Din_num), .en(1'b1), .Q(Din_out), .clk(clk), .clr(1'b0));
  Register #(.width(1)) Din_2 (.D(rd_only), .en(1'b1), .Q(rd_only_2), .clk(clk), .clr(1'b0));
  Register #(.width(32)) u_ALu (.D(ALU), .en(1'b1), .Q(ALU_out), .clk(clk), .clr(1'b0));
  Register #(.width(32)) ALu_2 (.D(MEM), .en(1'b1), .Q(MEM_out), .clk(clk), .clr(1'b0));
  Register #(.width(1)) Din_3 (.D(halt), .en(1'b1), .Q(halt_2), .clk(clk), .clr(1'b0));
endmodule

module W_Choice (
  input  [31:0] IR,
  input  [1:0] in_2,
  output [4:0] W__out,
  output lw
);

  wire not_1_out, not_2_out, not_3_out, not_4_out, specialchoice_1_j;
  wire [5:0] specialchoice_1_out;

  SpecialChoice specialchoice_1 (.Hi6(IR[31:26]), .Lo6(IR[5:0]), .J(specialchoice_1_j), .Out(specialchoice_1_out));
  Multiplexer #(.select(2), .width(5), .disabled(0), .enable("false")) multiplexer_1 (
    .in0(IR[15:11]), .in1(IR[20:16]), .in2({5{1'b1}}), .in3({5{1'b1}}), .out(W__out), .sel(in_2));
  not not_1 (not_1_out, specialchoice_1_j);
  not not_2 (not_2_out, specialchoice_1_out[4]);
  not not_3 (not_3_out, specialchoice_1_out[3]);
  not not_4 (not_4_out, specialchoice_1_out[2]);
  and and_1 (lw, not_1_out, specialchoice_1_out[5], not_2_out, not_3_out, not_4_out, specialchoice_1_out[1], specialchoice_1_out[0]);
endmodule

// out
module JudgeDataArgue (
  input  [4:0] R1,
  input  [4:0] R2,
  input  [4:0] _2_W,
  input  [4:0] _3_W,
  input  _2_rd,
  input  _3_rd,
  input  R1NoUse,
  input  R2NoUse,
  input  _2_bLW,
  input  bSW,
  output [1:0] R1_Choice,
  output [1:0] R2_Choice,
  output Load_Use,
  output bMemChoic,
  output b_2_choice
);

  wire and_1_out, and_2_out, and_3_out, and_4_out, comparator_1_eq, comparator_2_eq, comparator_3_eq,
       comparator_4_eq, comparator_5_eq, comparator_6_eq, not_1_out, not_2_out, not_3_out, not_4_out,
       not_5_out, not_6_out, not_7_out, not_8_out, not_9_out, or_1_out, or_3_out;

  not not_1 (not_1_out, _2_rd);
  not not_2 (not_2_out, _3_rd);
  not not_3 (not_3_out, R1NoUse);
  not not_4 (not_4_out, R2NoUse);
  Comparator #(.width(5)) comparator_1 (.a(R1), .b({5{1'b0}}), .eq(comparator_1_eq));  // open: gt, lt
  Comparator #(.width(5)) comparator_2 (.a(R2), .b({5{1'b0}}), .eq(comparator_2_eq));  // open: gt, lt
  not not_5 (not_5_out, comparator_1_eq);
  not not_6 (not_6_out, comparator_2_eq);
  Comparator #(.width(5)) comparator_3 (.a(R1), .b(_2_W), .eq(comparator_3_eq));  // open: gt, lt
  Comparator #(.width(5)) comparator_4 (.a(R1), .b(_3_W), .eq(comparator_4_eq));  // open: gt, lt
  Comparator #(.width(5)) comparator_5 (.a(R2), .b(_2_W), .eq(comparator_5_eq));  // open: gt, lt
  Comparator #(.width(5)) comparator_6 (.a(R2), .b(_3_W), .eq(comparator_6_eq));  // open: gt, lt
  and and_1 (and_1_out, not_1_out, not_5_out, comparator_3_eq, not_3_out);
  and and_2 (and_2_out, not_2_out, not_5_out, comparator_4_eq, not_3_out);
  and and_3 (and_3_out, not_1_out, not_6_out, comparator_5_eq, not_4_out);
  and and_4 (and_4_out, not_2_out, not_6_out, comparator_6_eq, not_4_out);
  and and_5 (bMemChoic, bSW, and_3_out);
  and and_6 (b_2_choice, and_4_out, bSW);
  not not_7 (not_7_out, and_1_out);
  not not_8 (not_8_out, and_3_out);
  or or_1 (or_1_out, and_3_out, and_1_out);
  or or_2 (R1_Choice[1], and_1_out, and_2_out);
  and and_7 (R1_Choice[0], not_7_out, and_2_out);
  or or_3 (or_3_out, and_3_out, and_4_out);
  and and_8 (R2_Choice[0], not_8_out, and_4_out);
  not not_9 (not_9_out, bSW);
  and and_9 (Load_Use, or_1_out, _2_bLW);
  and and_10 (R2_Choice[1], or_3_out, not_9_out);

  // Notes on the sheet:
  //   buff2
  //   buff3
  //   buff2
  //   buff3
endmodule
