// Logisim project 杨晓刚_CS1301_U201314791_regfile.circ as structural Verilog: 2 circuits, main circuit regfile
module regfile (
  input  [4:0] Reg1_num,
  input  [4:0] Reg2,
  input  [4:0] Write_Reg_num,
  input  [31:0] Din,
  input  Write_Enable,
  input  Clock,
  output [31:0] Reg1,
  output [31:0] s0_Value,
  output [31:0] s1_Value,
  output [31:0] s2_Value,
  output [31:0] ra_Value,
  output [31:0] Reg2_2
);

  _32reg u_32reg_1 (
    ._0(s0_Value), ._1(s1_Value), ._2(s2_Value), .R1(Reg1), ._3(ra_Value), .CLK(Clock), .R2(Reg2_2),
    .Din(Din), .W_num(Write_Reg_num), .WT_RD(Write_Enable), .R1_num(Reg1_num), .R2_num(Reg2));

  // Other names for the same wires on the sheet: clk = Clock; ra[31:0] = ra_Value; reg2_num[4:0] = Reg2;
  //   reg2_t[31:0] = Reg2_2; s0[31:0] = s0_Value; s1[31:0] = s1_Value; s2[31:0] = s2_Value; WE = Write_Enable;
  //   write_data[31:0] = Din

  // Notes on the sheet:
  //   输入引脚
  //   输出引脚
  //   请在下方利用上方输入输出引脚的隧道信号构建ALU电路，ctrl+d复制选择部件
  //   Debug引脚，便于观测寄存器值
  //   请勿修改引脚以及封装，直接使用隧道连接电路
endmodule

// $s0
module _32reg (
  input  [31:0] Din,
  input  CLK,
  input  [4:0] R1_num,
  input  [4:0] W_num,
  input  [4:0] R2_num,
  input  WT_RD,
  output [31:0] _0,
  output [31:0] _1,
  output [31:0] _2,
  output [31:0] _3,
  output [31:0] R1,
  output [31:0] R2
);

  wire and_1_out, decoder_1_out0, decoder_1_out1, decoder_1_out2, decoder_1_out3, decoder_1_out4,
       decoder_1_out5, decoder_1_out6, decoder_1_out7, decoder_1_out8, decoder_1_out9, decoder_1_out10,
       decoder_1_out11, decoder_1_out12, decoder_1_out13, decoder_1_out14, decoder_1_out15, decoder_1_out16,
       decoder_1_out17, decoder_1_out18, decoder_1_out19, decoder_1_out20, decoder_1_out21, decoder_1_out22,
       decoder_1_out23, decoder_1_out24, decoder_1_out25, decoder_1_out26, decoder_1_out27, decoder_1_out28,
       decoder_1_out29, decoder_1_out30, decoder_1_out31;
  wire [31:0] register_1_q, register_2_q, register_3_q, register_4_q, register_5_q, register_6_q,
       register_7_q, register_8_q, register_9_q, register_10_q, register_11_q, register_12_q, register_13_q,
       register_14_q, register_15_q, register_16_q, register_18_q, register_19_q, register_20_q,
       register_22_q, register_23_q, register_24_q, register_26_q, register_27_q, register_28_q,
       register_29_q, register_30_q, register_32_q;

  and and_1 (and_1_out, 1'b0, decoder_1_out0);
  Register #(.width(32), .trigger("falling")) register_1 (
    .D(Din), .en(and_1_out), .Q(register_1_q), .clk(CLK));  // open: clr
  Register #(.width(32), .trigger("falling")) register_2 (
    .D(Din), .en(decoder_1_out4), .Q(register_2_q), .clk(CLK));  // open: clr
  Register #(.width(32), .trigger("falling")) register_3 (
    .D(Din), .en(decoder_1_out8), .Q(register_3_q), .clk(CLK));  // open: clr
  Register #(.width(32), .trigger("falling")) register_4 (
    .D(Din), .en(decoder_1_out12), .Q(register_4_q), .clk(CLK));  // open: clr
  Decoder #(.select(5), .disabled(0)) decoder_1 (
    .out0(decoder_1_out0), .out1(decoder_1_out1), .out2(decoder_1_out2), .out3(decoder_1_out3),
    .out4(decoder_1_out4), .out5(decoder_1_out5), .out6(decoder_1_out6), .out7(decoder_1_out7),
    .out8(decoder_1_out8), .out9(decoder_1_out9), .out10(decoder_1_out10), .out11(decoder_1_out11),
    .out12(decoder_1_out12), .out13(decoder_1_out13), .out14(decoder_1_out14), .out15(decoder_1_out15),
    .out16(decoder_1_out16), .out17(decoder_1_out17), .out18(decoder_1_out18), .out19(decoder_1_out19),
    .out20(decoder_1_out20), .out21(decoder_1_out21), .out22(decoder_1_out22), .out23(decoder_1_out23),
    .out24(decoder_1_out24), .out25(decoder_1_out25), .out26(decoder_1_out26), .out27(decoder_1_out27),
    .out28(decoder_1_out28), .out29(decoder_1_out29), .out30(decoder_1_out30), .out31(decoder_1_out31),
    .sel(W_num), .en(WT_RD));
  Register #(.width(32), .trigger("falling")) register_5 (
    .D(Din), .en(decoder_1_out1), .Q(register_5_q), .clk(CLK));  // open: clr
  Register #(.width(32), .trigger("falling")) register_6 (
    .D(Din), .en(decoder_1_out5), .Q(register_6_q), .clk(CLK));  // open: clr
  Register #(.width(32), .trigger("falling")) register_7 (
    .D(Din), .en(decoder_1_out9), .Q(register_7_q), .clk(CLK));  // open: clr
  Register #(.width(32), .trigger("falling")) register_8 (
    .D(Din), .en(decoder_1_out13), .Q(register_8_q), .clk(CLK));  // open: clr
  Multiplexer #(.select(5), .width(32)) multiplexer_1 (
    .in0(register_1_q), .in1(register_5_q), .in2(register_9_q), .in3(register_13_q), .in4(register_2_q),
    .in5(register_6_q), .in6(register_10_q), .in7(register_14_q), .in8(register_3_q), .in9(register_7_q),
    .in10(register_11_q), .in11(register_15_q), .in12(register_4_q), .in13(register_8_q),
    .in14(register_12_q), .in15(register_16_q), .in16(_0), .in17(_1), .in18(_2), .in19(register_26_q),
    .in20(register_18_q), .in21(register_22_q), .in22(register_28_q), .in23(register_27_q),
    .in24(register_19_q), .in25(register_23_q), .in26(register_29_q), .in27(register_30_q),
    .in28(register_20_q), .in29(register_24_q), .in30(register_32_q), .in31(_3), .out(R1), .sel(R1_num),
    .en(1'b1));
  Register #(.width(32), .trigger("falling")) register_9 (
    .D(Din), .en(decoder_1_out2), .Q(register_9_q), .clk(CLK));  // open: clr
  Register #(.width(32), .trigger("falling")) register_10 (
    .D(Din), .en(decoder_1_out6), .Q(register_10_q), .clk(CLK));  // open: clr
  Register #(.width(32), .trigger("falling")) register_11 (
    .D(Din), .en(decoder_1_out10), .Q(register_11_q), .clk(CLK));  // open: clr
  Register #(.width(32), .trigger("falling")) register_12 (
    .D(Din), .en(decoder_1_out14), .Q(register_12_q), .clk(CLK));  // open: clr
  Register #(.width(32), .trigger("falling")) register_13 (
    .D(Din), .en(decoder_1_out3), .Q(register_13_q), .clk(CLK));  // open: clr
  Register #(.width(32), .trigger("falling")) register_14 (
    .D(Din), .en(decoder_1_out7), .Q(register_14_q), .clk(CLK));  // open: clr
  Register #(.width(32), .trigger("falling")) register_15 (
    .D(Din), .en(decoder_1_out11), .Q(register_15_q), .clk(CLK));  // open: clr
  Register #(.width(32), .trigger("falling")) register_16 (
    .D(Din), .en(decoder_1_out15), .Q(register_16_q), .clk(CLK));  // open: clr
  Register #(.width(32), .trigger("falling")) register_17 (
    .D(Din), .en(decoder_1_out16), .Q(_0), .clk(CLK));  // open: clr
  Register #(.width(32), .trigger("falling")) register_18 (
    .D(Din), .en(decoder_1_out20), .Q(register_18_q), .clk(CLK));  // open: clr
  Register #(.width(32), .trigger("falling")) register_19 (
    .D(Din), .en(decoder_1_out24), .Q(register_19_q), .clk(CLK));  // open: clr
  Register #(.width(32), .trigger("falling")) register_20 (
    .D(Din), .en(decoder_1_out28), .Q(register_20_q), .clk(CLK));  // open: clr
  Register #(.width(32), .trigger("falling")) register_21 (
    .D(Din), .en(decoder_1_out17), .Q(_1), .clk(CLK));  // open: clr
  Register #(.width(32), .trigger("falling")) register_22 (
    .D(Din), .en(decoder_1_out21), .Q(register_22_q), .clk(CLK));  // open: clr
  Register #(.width(32), .trigger("falling")) register_23 (
    .D(Din), .en(decoder_1_out25), .Q(register_23_q), .clk(CLK));  // open: clr
  Register #(.width(32), .trigger("falling")) register_24 (
    .D(Din), .en(decoder_1_out29), .Q(register_24_q), .clk(CLK));  // open: clr
  Register #(.width(32), .trigger("falling")) register_25 (
    .D(Din), .en(decoder_1_out18), .Q(_2), .clk(CLK));  // open: clr
  Register #(.width(32), .trigger("falling")) register_26 (
    .D(Din), .en(decoder_1_out19), .Q(register_26_q), .clk(CLK));  // open: clr
  Register #(.width(32), .trigger("falling")) register_27 (
    .D(Din), .en(decoder_1_out23), .Q(register_27_q), .clk(CLK));  // open: clr
  Register #(.width(32), .trigger("falling")) register_28 (
    .D(Din), .en(decoder_1_out22), .Q(register_28_q), .clk(CLK));  // open: clr
  Register #(.width(32), .trigger("falling")) register_29 (
    .D(Din), .en(decoder_1_out26), .Q(register_29_q), .clk(CLK));  // open: clr
  Register #(.width(32), .trigger("falling")) register_30 (
    .D(Din), .en(decoder_1_out27), .Q(register_30_q), .clk(CLK));  // open: clr
  Register #(.width(32), .trigger("falling")) register_31 (
    .D(Din), .en(decoder_1_out31), .Q(_3), .clk(CLK));  // open: clr
  Register #(.width(32), .trigger("falling")) register_32 (
    .D(Din), .en(decoder_1_out30), .Q(register_32_q), .clk(CLK));  // open: clr
  Multiplexer #(.select(5), .width(32)) multiplexer_2 (
    .in0(register_1_q), .in1(register_5_q), .in2(register_9_q), .in3(register_13_q), .in4(register_2_q),
    .in5(register_6_q), .in6(register_10_q), .in7(register_14_q), .in8(register_3_q), .in9(register_7_q),
    .in10(register_11_q), .in11(register_15_q), .in12(register_4_q), .in13(register_8_q),
    .in14(register_12_q), .in15(register_16_q), .in16(_0), .in17(_1), .in18(_2), .in19(register_26_q),
    .in20(register_18_q), .in21(register_22_q), .in22(register_28_q), .in23(register_27_q),
    .in24(register_19_q), .in25(register_23_q), .in26(register_29_q), .in27(register_30_q),
    .in28(register_20_q), .in29(register_24_q), .in30(register_32_q), .in31(_3), .out(R2), .sel(R2_num),
    .en(1'b1));

  // Other names for the same wires on the sheet: clock = CLK; s0[31:0] = _0; s1[31:0] = _1; s2[31:0] = _2;
  //   s3[31:0] = _3; W_R = WT_RD
endmodule
