// Logisim project 杨晓刚_CS1301_U201314791_alu.circ as structural Verilog: 4 circuits, main circuit ALU
module ALU (
  input  [31:0] X,
  input  [31:0] Y,
  input  [3:0] AluOP,
  output Signed_Overflow,
  output UnSigned_Overflow,
  output Equal,
  output [31:0] Result,
  output [31:0] Result_2
);

  wire AddCF, AddOF, comparator_2_lt, comparator_3_lt, SubCF, SubOF;
  wire [31:0] Add, Div1, Div2, MulH, MulL, \nor , \signed , Sub, tunnel, tunnel_t, tunnel_t_t, tunnel_t_t_t,
       tunnel_t_t_t_t, usigned, \xor ;

  // Probe on X
  // Probe on X
  Comparator #(.width(32)) comparator_1 (.a(X), .b(Y), .eq(Equal));  // open: gt, lt
  Comparator #(.width(32)) comparator_2 (.a(X), .b(Y), .lt(comparator_2_lt));  // open: gt, eq
  // Probe on Y
  // Probe on Y
  Shifter #(.width(32), .shift("lr")) shifter_1 (.in(X), .\dist (Y[4:0]), .out(tunnel_t_t_t));
  Multiplier #(.width(32)) multiplier_1 (.a(X), .b(Y), .out(MulL), .cin({32{1'b0}}), .cout(MulH));
  add add_1 (.in_1(X), .in_2(Y), .out(Add), .\高位进位 (AddCF), .OF(AddOF));
  assign tunnel = X & Y;  // AND_Gate and_1, 32 bits wide
  assign \xor  = X ^ Y;  // XOR_Gate xor_1, 32 bits wide
  assign \signed  = {{31{1'b0}}, comparator_2_lt};  // Bit_Extender bit_extender_1
  Multiplexer #(.select(4), .width(32)) multiplexer_1 (
    .in0(tunnel_t), .in1(tunnel_t_t_t), .in2(tunnel_t_t), .in3(MulL), .in4(Div1), .in5(Add), .in6(Sub),
    .in7(tunnel), .in8(tunnel_t_t_t_t), .in9(\xor ), .in10(\nor ), .in11(\signed ), .in12(usigned),
    .in13({32{1'b0}}), .in14({32{1'b0}}), .in15({32{1'b0}}), .out(Result), .sel(AluOP), .en(1'b1));
  Multiplexer #(.select(4)) multiplexer_2 (
    .in0(1'b0), .in1(1'b0), .in2(1'b0), .in3(1'b0), .in4(1'b0), .in5(AddOF), .in6(SubOF), .in7(1'b0),
    .in8(1'b0), .in9(1'b0), .in10(1'b0), .in11(1'b0), .in12(1'b0), .in13(1'b0), .in14(1'b0), .in15(1'b0),
    .out(Signed_Overflow), .sel(AluOP), .en(1'b1));
  // Probe on AluOP
  // Probe on Result
  // Probe on Result
  Shifter #(.width(32)) shifter_2 (.in(X), .\dist (Y[4:0]), .out(tunnel_t));
  sub sub_1 (.in_1(X), .in_2(Y), .out(Sub), .\高位借位 (SubCF), .OF(SubOF));
  Comparator #(.width(32), .mode("unsigned")) comparator_3 (.a(X), .b(Y), .lt(comparator_3_lt));  // open: gt, eq
  Shifter #(.width(32), .shift("ar")) shifter_3 (.in(X), .\dist (Y[4:0]), .out(tunnel_t_t));
  Divider #(.width(32)) divider_1 (.a(X), .b(Y), .out(Div1), .upper({32{1'b0}}), .rem(Div2));
  assign tunnel_t_t_t_t = X | Y;  // OR_Gate or_1, 32 bits wide
  assign \nor  = ~(X | Y);  // NOR_Gate nor_1, 32 bits wide
  assign usigned = {{31{1'b0}}, comparator_3_lt};  // Bit_Extender bit_extender_2
  // Probe on Result_2
  Multiplexer #(.select(4), .width(32)) multiplexer_3 (
    .in0({32{1'b0}}), .in1({32{1'b0}}), .in2({32{1'b0}}), .in3(MulH), .in4(Div2), .in5({32{1'b0}}),
    .in6({32{1'b0}}), .in7({32{1'b0}}), .in8({32{1'b0}}), .in9({32{1'b0}}), .in10({32{1'b0}}),
    .in11({32{1'b0}}), .in12({32{1'b0}}), .in13({32{1'b0}}), .in14({32{1'b0}}), .in15({32{1'b0}}),
    .out(Result_2), .sel(AluOP), .en(1'b1));
  Multiplexer #(.select(4)) multiplexer_4 (
    .in0(1'b0), .in1(1'b0), .in2(1'b0), .in3(1'b0), .in4(1'b0), .in5(AddCF), .in6(SubCF), .in7(1'b0),
    .in8(1'b0), .in9(1'b0), .in10(1'b0), .in11(1'b0), .in12(1'b0), .in13(1'b0), .in14(1'b0), .in15(1'b0),
    .out(UnSigned_Overflow), .sel(AluOP), .en(1'b1));

  // Other names for the same wires on the sheet: CF = UnSigned_Overflow; OF = Signed_Overflow;
  //   Result2[31:0] = Result_2; S[3:0] = AluOP

  // Notes on the sheet:
  //   判断相等
  //   逻辑右移
  //   乘法
  //   加法
  //   与运算
  //   异或运算
  //   有符号比较
  //   输入引脚
  //   高位
  //   低位
  //   请在下方利用上方输入输出引脚的隧道信号构建ALU电路，ctrl+d复制选择部件
  //   华中科技大学计算机学院 计算机组成原理，鸣谢加州大学伯克利CS61C课程
  //   逻辑左移
  //   算术右移
  //   减法
  //   或运算
  //   或非运算
  //   无符号比较
  //   除法
  //   商
  //   余数
  //   输出引脚
  //   探测区域
endmodule

module \演示电路  (
  input  [31:0] X,
  input  [31:0] Y,
  input  [3:0] ALUOP,
  output Signed_Overflow,
  output Unsigned_overflow,
  output [31:0] Result,
  output [31:0] Result_2,
  output Equal
);

  // Probe on X
  // Probe on X
  ALU alu_1 (
    .AluOP(ALUOP), .X(X), .Equal(Equal), .Result(Result), .Signed_Overflow(Signed_Overflow), .Y(Y),
    .Result_2(Result_2), .UnSigned_Overflow(Unsigned_overflow));
  // Probe on ALUOP
  // Probe on Y
  // Probe on Y
  // Probe on Result
  // Probe on Result
  // Probe on Result_2
endmodule

module add (
  input  [31:0] in_1,
  input  [31:0] in_2,
  output [31:0] out,
  output \高位进位 ,
  output OF
);

  wire not_1_out, xor_1_out, \异号_out ;

  Adder #(.width(32)) adder_1 (.a(in_1), .b(in_2), .out(out), .cin(1'b0), .cout(\高位进位 ));
  xor xor_1 (xor_1_out, in_1[31], in_2[31]);
  xor \u_异号  (\异号_out , in_2[31], out[31]);
  not not_1 (not_1_out, xor_1_out);
  and and_1 (OF, not_1_out, \异号_out );

  // Other names for the same wires on the sheet: x[31:0] = in_1; y[31:0] = in_2

  // Notes on the sheet:
  //   溢出
  //   正数+正数=负数
  //   负数+负数=正数
endmodule

module sub (
  input  [31:0] in_1,
  input  [31:0] in_2,
  output [31:0] out,
  output \高位借位 ,
  output OF
);

  wire xor_1_out, xor_2_out;

  Subtractor #(.width(32)) subtractor_1 (.a(in_1), .b(in_2), .out(out), .bin(1'b0), .bout(\高位借位 ));
  xor xor_1 (xor_1_out, in_2[31], in_1[31]);
  xor xor_2 (xor_2_out, in_1[31], out[31]);
  and and_1 (OF, xor_1_out, xor_2_out);

  // Other names for the same wires on the sheet: x[31:0] = in_1; y[31:0] = in_2

  // Notes on the sheet:
  //   溢出
  //   负数-正数＝正数
  //   正数－负数＝负数
endmodule
