// Logisim project 杨晓刚_CS1301_U201314791_cpu.circ as structural Verilog: 7 circuits, main circuit main
module main (
  input  in_1
);

  wire and_2_out, bArithmetic, bEqual, bLW, bSW, clock, clock_1_out, control_1_b_beq_bne, control_1_beq,
       control_1_bimme, \control_1_停机 , not_1_out, not_2_out, not_3_out, or_1_out, xnor_1_out;
  wire [3:0] control_1_choice;
  wire [4:0] base_LW_SW, control_1_xreg, control_1_yreg, multiplexer_1_out, multiplexer_2_out,
       multiplexer_6_out, resualtReg, rt;
  wire [9:0] bit_extender_1_out;
  wire [15:0] adder_1_out, adder_2_out, adder_3_out, bit_extender_3_out, JMPWHERE, multiplexer_4_out, PC_q,
       RAMaddr;
  wire [31:0] ALU_result, bit_extender_2_out, multiplexer_3_out, multiplexer_5_out, n32reg_1__0, n32reg_1__1,
       n32reg_1__2, n32reg_1__3, n32reg_1_r1, n32reg_1_r2, ram_1_data, rom_1_data;

  and and_1 (clock, clock_1_out, not_1_out);
  Clock clock_1 (.out(clock_1_out));
  not not_1 (not_1_out, \control_1_停机 );
  // Probe on RAMaddr
  Register #(.width(16)) PC (.D(multiplexer_4_out), .en(1'b1), .Q(PC_q), .clk(clock), .clr(in_1));
  Adder #(.width(16)) adder_1 (.a(PC_q), .b(16'h1), .out(adder_1_out));  // open: cin, cout
  Bit_Extender #(.in_width(16), .out_width(10)) bit_extender_1 (.in(PC_q), .out(bit_extender_1_out));
  or or_1 (or_1_out, bLW, bSW);
  // Probe on ram_1_data
  Adder #(.width(16)) adder_2 (.a(JMPWHERE), .b(PC_q), .out(adder_2_out));  // open: cin, cout
  Multiplexer #(.width(5)) multiplexer_1 (
    .in0(control_1_xreg), .in1(base_LW_SW), .out(multiplexer_1_out), .sel(or_1_out), .en(1'b1));
  Adder #(.width(16)) adder_3 (.a(adder_2_out), .b(16'h1), .out(adder_3_out));  // open: cin, cout
  ROM #(.addrWidth(10), .dataWidth(32)) rom_1 (.addr(bit_extender_1_out), .data(rom_1_data), .sel(1'b1));
  Multiplexer #(.width(5)) multiplexer_2 (.in0(resualtReg), .in1(rt), .out(multiplexer_2_out), .sel(bLW), .en(1'b1));
  RAM #(.addrWidth(16), .dataWidth(32)) ram_1 (
    .addr(RAMaddr), .data(ram_1_data), .sel(1'b1), .clk(clock), .ld(not_2_out));  // open: clr
  Multiplexer #(.width(32)) multiplexer_3 (
    .in0(ALU_result), .in1(ram_1_data), .out(multiplexer_3_out), .sel(bLW), .en(1'b1));
  assign ram_1_data = bSW ? n32reg_1_r2 : 32'bz;  // Controlled_Buffer controlled_buffer_1
  not not_2 (not_2_out, bSW);
  // Probe on ram_1_data
  and and_2 (and_2_out, control_1_b_beq_bne, xnor_1_out);
  xnor xnor_1 (xnor_1_out, control_1_beq, bEqual);
  Multiplexer #(.width(16)) multiplexer_4 (
    .in0(adder_1_out), .in1(adder_3_out), .out(multiplexer_4_out), .sel(and_2_out), .en(1'b1));
  _32reg u_32reg_1 (
    ._0(n32reg_1__0), ._1(n32reg_1__1), ._2(n32reg_1__2), .R1(n32reg_1_r1), ._3(n32reg_1__3), .CLK(clock),
    .R2(n32reg_1_r2), .Din(multiplexer_3_out), .W_num(multiplexer_2_out), .WT_RD(not_3_out),
    .R1_num(multiplexer_1_out), .R2_num(multiplexer_6_out));
  not not_3 (not_3_out, bSW);
  control control_1 (
    .in_1(rom_1_data), .\停机 (\control_1_停机 ), .PC_chang_ADDI(JMPWHERE), .choice(control_1_choice),
    .xReg(control_1_xreg), .yReg(control_1_yreg), .bImme(control_1_bimme), .resultReg(resualtReg),
    .b_beq_bne(control_1_b_beq_bne), .bArithmetic(bArithmetic), .base(base_LW_SW), .bLW(bLW), .bSW(bSW),
    .rt(rt), .bEQ(control_1_beq));
  // Probe on n32reg_1__0
  // Probe on n32reg_1__1
  // Probe on n32reg_1__2
  // Probe on n32reg_1__3
  assign bit_extender_2_out = {{16{JMPWHERE[15]}}, JMPWHERE};  // Bit_Extender bit_extender_2
  Multiplexer #(.width(32)) multiplexer_5 (
    .in0(n32reg_1_r2), .in1(bit_extender_2_out), .out(multiplexer_5_out), .sel(control_1_bimme), .en(1'b1));
  ALU alu_1 (
    .AluOP(control_1_choice), .X(n32reg_1_r1), .Equal(bEqual), .Result(ALU_result), .Y(multiplexer_5_out));  // open: Signed_Overflow, Result_2, UnSigned_Overflow
  Multiplexer #(.width(5)) multiplexer_6 (
    .in0(control_1_yreg), .in1(rt), .out(multiplexer_6_out), .sel(bSW), .en(1'b1));
  Bit_Extender #(.in_width(32)) bit_extender_3 (.in(n32reg_1_r1), .out(bit_extender_3_out));
  // Probe on ALU_result
  Shifter #(.width(16), .shift("lr")) shifter_1 (.in(bit_extender_3_out), .\dist (4'b0010), .out(RAMaddr));

  // Notes on the sheet:
  //   R1选择区域
  //   RAM
  //   PC跳转区域
  //   ROM 指令存储
  //   contents of rom_1 (hex, n*v repeats v):
  //   2010ffff 20110000 ae300000 22100001 22310004 ae300000 22100001 22310004 ae300000 22100001 22310004
  //   ae300000 22100001 22310004 ae300000 22100001 22310004 ae300000 22100001 22310004 ae300000 22100001
  //   22310004 ae300000 22100001 22310004 ae300000 22100001 22310004 ae300000 22100001 22310004 ae300000
  //   22100001 22310004 ae300000 22100001 22310004 ae300000 22100001 22310004 ae300000 22100001 22310004
  //   ae300000 22100001 22310004 ae300000 22100001 22310004 22100001 8020 2011003c 8e130000 8e340000
  //   274402a 11000002 ae330000 ae140000 2231fffc 1611fff8 22100004 2011003c 1611fff5 2002000a c
  //   W#选择区域
  //   Din选择
  //   control 模块
  //   ALU模块
  //   各种信号
  //   R2选择区域
  //   地址转化
endmodule

module control (
  input  [31:0] in_1,
  output \停机 ,
  output [3:0] choice,
  output bImme,
  output [15:0] PC_chang_ADDI,
  output bArithmetic,
  output b_beq_bne,
  output bEQ,
  output bLW,
  output bSW,
  output [4:0] rt,
  output [4:0] base,
  output [4:0] resultReg,
  output [4:0] yReg,
  output [4:0] xReg
);

  wire add_slt, n3_choose_1_add, n3_choose_1_slt, n6_choose_1_bne, n6_choose_1_special, or_2_out;
  wire [5:0] mux_2x6bit_to_1_1_out;

  _6_choose u_6_choose_1 (
    .i0(in_1[31]), .i1(in_1[30]), .i2(in_1[29]), .i3(in_1[28]), .i4(in_1[27]), .i5(in_1[26]),
    .special(n6_choose_1_special), .addi(bImme), .beq(bEQ), .bne(n6_choose_1_bne), .lw(bLW), .sw(bSW));
  MUX_2x6bit_to_1 mux_2x6bit_to_1_1 (
    ._0({6{1'b0}}), ._1(in_1[5:0]), .choice(n6_choose_1_special), .out(mux_2x6bit_to_1_1_out));
  _3_choose u_3_choose_1 (
    .i0(mux_2x6bit_to_1_1_out[5]), .i1(mux_2x6bit_to_1_1_out[4]), .i2(mux_2x6bit_to_1_1_out[3]),
    .i3(mux_2x6bit_to_1_1_out[2]), .i4(mux_2x6bit_to_1_1_out[1]), .i5(mux_2x6bit_to_1_1_out[0]),
    .add(n3_choose_1_add), .slt(n3_choose_1_slt), .syscal(\停机 ));
  or or_1 (b_beq_bne, bEQ, n6_choose_1_bne);
  or or_2 (or_2_out, n3_choose_1_add, bImme);
  or or_3 (add_slt, n3_choose_1_add, n3_choose_1_slt);
  chooseArithmetic choosearithmetic_1 (
    .add_addi(or_2_out), .beq_bne(b_beq_bne), .slt(n3_choose_1_slt), .choice(choice));
  or or_4 (bArithmetic, n3_choose_1_slt, or_2_out, b_beq_bne);
  outReg outreg_1 (
    .rt(in_1[20:16]), .rd(in_1[15:11]), .add_slt(add_slt), .addi(bImme), .bne_beq(b_beq_bne), .out(resultReg));

  assign base = in_1[25:21];
  assign PC_chang_ADDI = in_1[15:0];
  assign rt = in_1[20:16];
  assign xReg = in_1[25:21];
  assign yReg = in_1[20:16];

  // Notes on the sheet:
  //   ADDI
  //   BEQ
  //   BNE
  //   LW
  //   SW
  //   ADD
  //   SLT
  //   SYSCALL
endmodule

module MUX_2x6bit_to_1 (
  input  [5:0] _0,
  input  [5:0] _1,
  input  choice,
  output [5:0] out
);

  wire not_1_out;
  wire [5:0] and_1_out, and_2_out, bit_extender_1_out, bit_extender_2_out;

  not not_1 (not_1_out, choice);
  assign bit_extender_1_out = {{5{not_1_out}}, not_1_out};  // Bit_Extender bit_extender_1
  assign bit_extender_2_out = {{5{choice}}, choice};  // Bit_Extender bit_extender_2
  assign and_1_out = _0 & bit_extender_1_out;  // AND_Gate and_1, 6 bits wide
  assign and_2_out = _1 & bit_extender_2_out;  // AND_Gate and_2, 6 bits wide
  assign out = and_1_out | and_2_out;  // OR_Gate or_1, 6 bits wide
endmodule

module chooseArithmetic (
  input  add_addi,
  input  beq_bne,
  input  slt,
  output [3:0] choice
);

  wire [3:0] and_1_out, and_2_out, and_3_out, bit_extender_1_out, bit_extender_2_out, bit_extender_3_out;

  assign bit_extender_1_out = {{3{add_addi}}, add_addi};  // Bit_Extender bit_extender_1
  assign bit_extender_2_out = {{3{beq_bne}}, beq_bne};  // Bit_Extender bit_extender_2
  assign bit_extender_3_out = {{3{slt}}, slt};  // Bit_Extender bit_extender_3
  assign and_1_out = bit_extender_1_out & 4'b0101;  // AND_Gate and_1, 4 bits wide
  assign and_2_out = bit_extender_2_out & 4'b0110;  // AND_Gate and_2, 4 bits wide
  assign and_3_out = bit_extender_3_out & 4'b1011;  // AND_Gate and_3, 4 bits wide
  assign choice = and_1_out | and_2_out | and_3_out;  // OR_Gate or_1, 4 bits wide
endmodule

module outReg (
  input  [4:0] rt,
  input  [4:0] rd,
  input  add_slt,
  input  addi,
  input  bne_beq,
  output [4:0] out
);

  wire [4:0] and_1_out, and_2_out, and_3_out, bit_extender_1_out, bit_extender_2_out, bit_extender_3_out;

  assign bit_extender_1_out = {{4{add_slt}}, add_slt};  // Bit_Extender bit_extender_1
  assign bit_extender_2_out = {{4{addi}}, addi};  // Bit_Extender bit_extender_2
  assign bit_extender_3_out = {{4{bne_beq}}, bne_beq};  // Bit_Extender bit_extender_3
  assign and_1_out = rd & bit_extender_1_out;  // AND_Gate and_1, 5 bits wide
  assign and_2_out = rt & bit_extender_2_out;  // AND_Gate and_2, 5 bits wide
  assign and_3_out = {5{1'b0}} & bit_extender_3_out;  // AND_Gate and_3, 5 bits wide
  assign out = and_1_out | and_2_out | and_3_out;  // OR_Gate or_1, 5 bits wide
endmodule

module _6_choose (
  input  i0,
  input  i1,
  input  i2,
  input  i3,
  input  i4,
  input  i5,
  output special,
  output addi,
  output beq,
  output bne,
  output lw,
  output sw
);

  wire not_1_out, not_2_out, not_3_out, not_4_out, not_5_out, not_6_out, not_7_out, not_8_out, not_9_out,
       not_10_out, not_11_out, not_12_out, not_13_out, not_14_out, not_15_out, not_16_out, not_17_out,
       not_18_out, not_19_out, not_20_out, not_21_out, not_22_out, not_23_out, not_24_out, not_25_out;

  not not_1 (not_1_out, i0);
  not not_2 (not_2_out, i1);
  not not_3 (not_3_out, i2);
  not not_4 (not_4_out, i3);
  not not_5 (not_5_out, i4);
  not not_6 (not_6_out, i5);
  not not_7 (not_7_out, i0);
  not not_8 (not_8_out, i1);
  not not_9 (not_9_out, i3);
  not not_10 (not_10_out, i4);
  not not_11 (not_11_out, i5);
  not not_12 (not_12_out, i0);
  not not_13 (not_13_out, i1);
  not not_14 (not_14_out, i2);
  not not_15 (not_15_out, i4);
  not not_16 (not_16_out, i5);
  not not_17 (not_17_out, i0);
  not not_18 (not_18_out, i1);
  not not_19 (not_19_out, i2);
  not not_20 (not_20_out, i4);
  not not_21 (not_21_out, i1);
  not not_22 (not_22_out, i2);
  not not_23 (not_23_out, i3);
  not not_24 (not_24_out, i1);
  not not_25 (not_25_out, i3);
  and and_1 (special, not_1_out, not_2_out, not_3_out, not_4_out, not_5_out, not_6_out);
  and and_2 (addi, not_7_out, not_8_out, i2, not_9_out, not_10_out, not_11_out);
  and and_3 (beq, not_12_out, not_13_out, not_14_out, i3, not_15_out, not_16_out);
  and and_4 (bne, not_17_out, not_18_out, not_19_out, i3, not_20_out, i5);
  and and_5 (lw, i0, not_21_out, not_22_out, not_23_out, i4, i5);
  and and_6 (sw, i0, not_24_out, i2, not_25_out, i4, i5);
endmodule

module _3_choose (
  input  i0,
  input  i1,
  input  i2,
  input  i3,
  input  i4,
  input  i5,
  output add,
  output slt,
  output syscal
);

  wire not_1_out, not_2_out, not_3_out, not_4_out, not_5_out, not_6_out, not_7_out, not_8_out, not_9_out,
       not_10_out, not_11_out, not_12_out;

  not not_1 (not_1_out, i1);
  not not_2 (not_2_out, i2);
  not not_3 (not_3_out, i3);
  not not_4 (not_4_out, i4);
  not not_5 (not_5_out, i5);
  not not_6 (not_6_out, i1);
  not not_7 (not_7_out, i3);
  not not_8 (not_8_out, i5);
  not not_9 (not_9_out, i0);
  not not_10 (not_10_out, i1);
  not not_11 (not_11_out, i4);
  not not_12 (not_12_out, i5);
  and and_1 (add, i0, not_1_out, not_2_out, not_3_out, not_4_out, not_5_out);
  and and_2 (slt, i0, not_6_out, i2, not_7_out, i4, not_8_out);
  and and_3 (syscal, not_9_out, not_10_out, i2, i3, not_11_out, not_12_out);
endmodule
