// Logisim project 杨晓刚_CS1301_U201314791_实验一附加题.circ as structural Verilog: 1 circuit, main circuit main
module main (
  input  \初始值 ,
  input  \输入区域 ,
  input  in_3
);

  wire bStop, clk, not_1_out, not_2_out;
  wire [31:0] _1, _2, a, alu_1_result, ans, multiplexer_2_out;

  Clock \u_时钟  (.out(clk));
  // Probe on a
  // Probe on ans
  Multiplexer #(.width(32)) multiplexer_1 (.in0(32'h1), .in1(32'h2), .out(a), .sel(\初始值 ), .en(1'b1));
  Multiplexer #(.width(32)) multiplexer_2 (.in0(32'h9), .in1(32'h12), .out(multiplexer_2_out), .sel(\初始值 ), .en(1'b1));
  Comparator #(.width(32)) comparator_1 (.a(multiplexer_2_out), .b(_2), .eq(bStop));  // open: gt, lt
  // Probe on _2
  // Probe on bStop
  Register #(.width(32)) register_1 (.D(alu_1_result), .en(not_1_out), .Q(ans), .clk(clk), .clr(in_3));
  not not_1 (not_1_out, bStop);
  Hex_Digit_Display hex_digit_display_1 (.value(ans[15:12]));  // open: dp
  ALU alu_1 (
    .AluOP(4'b0101), .X(ans), .Result(alu_1_result), .Y(_2));  // open: Equal, Signed_Overflow, Result_2, UnSigned_Overflow
  Hex_Digit_Display hex_digit_display_2 (.value(ans[11:8]));  // open: dp
  Hex_Digit_Display hex_digit_display_3 (.value(ans[7:4]));  // open: dp
  Hex_Digit_Display hex_digit_display_4 (.value(ans[3:0]));  // open: dp
  Adder #(.width(32)) adder_1 (.a(a), .b(_2), .out(_1), .cin(1'b0));  // open: cout
  not not_2 (not_2_out, bStop);
  Register #(.width(32)) register_2 (.D(_1), .en(not_2_out), .Q(_2), .clk(clk), .clr(\输入区域 ));

  // Other names for the same wires on the sheet: input = \初始值 ; Regist1Clear = \输入区域 ; Regist2Clear = in_3

  // Notes on the sheet:
  //   判断差值
  //   停止累加条件
  //   值查看区域
  //   清空寄存器1
  //   清空寄存器2
  //   寄存器2 累加和
  //   16进制数码管显示区域
  //   累加计算
  //   寄存器1
  //   存储下次累加的值
endmodule
