// Logisim project 杨晓刚_CS1301_U201314791_实验二附加题.circ as structural Verilog: 1 circuit, main circuit main
module main (
  input  \RAM清零 ,
  input  \计数器清零 
);

  wire clock_1_out, comparator_1_gt, not_1_out, not_2_out;
  wire [4:0] adder_1_out, controlled_buffer_1_out, counter_1_q, subtractor_1_out;
  wire [15:0] bit_extender_1_out, ram_1_data;
  wire [31:0] alu_1_result, ans, n32reg_1_r1, n32reg_1_r2;

  Clock clock_1 (.out(clock_1_out));
  Counter #(.width(5), .max('h1f), .ongoal("stay")) counter_1 (
    .Q(counter_1_q), .clk(clock_1_out), .clr(\计数器清零 ));  // open: load, D, count, carry
  Comparator #(.width(5), .mode("unsigned")) comparator_1 (
    .a(counter_1_q), .b(5'b01111), .gt(comparator_1_gt));  // open: eq, lt
  Adder #(.width(5)) adder_1 (.a(counter_1_q), .b(5'b00001), .out(adder_1_out));  // open: cin, cout
  Subtractor #(.width(5)) subtractor_1 (.a(counter_1_q), .b(5'b01111), .out(subtractor_1_out));  // open: bin, bout
  not not_1 (not_1_out, comparator_1_gt);
  RAM #(.addrWidth(5), .dataWidth(16)) ram_1 (
    .addr(counter_1_q), .data(ram_1_data), .sel(1'b1), .clk(clock_1_out), .ld(not_1_out), .clr(\RAM清零 ));
  assign controlled_buffer_1_out = comparator_1_gt ? subtractor_1_out : 5'bz;  // Controlled_Buffer controlled_buffer_1
  assign ram_1_data = comparator_1_gt ? bit_extender_1_out : 16'bz;  // Controlled_Buffer controlled_buffer_2
  Bit_Extender #(.in_width(32), .\type ("sign")) bit_extender_1 (.in(n32reg_1_r2), .out(bit_extender_1_out));
  assign ans = {{16{ram_1_data[15]}}, ram_1_data};  // Bit_Extender bit_extender_2
  not not_2 (not_2_out, comparator_1_gt);
  _32reg u_32reg_1 (
    .R1(n32reg_1_r1), .CLK(clock_1_out), .R2(n32reg_1_r2), .Din(alu_1_result), .W_num(adder_1_out),
    .WT_RD(not_2_out), .R1_num(counter_1_q), .R2_num(controlled_buffer_1_out));  // open: _0, _1, _2, _3
  Hex_Digit_Display hex_digit_display_1 (.value(ans[15:12]));  // open: dp
  Hex_Digit_Display hex_digit_display_2 (.value(ans[11:8]));  // open: dp
  ALU alu_1 (
    .AluOP(4'b0101), .X(n32reg_1_r1), .Result(alu_1_result), .Y(ans));  // open: Equal, Signed_Overflow, Result_2, UnSigned_Overflow
  Hex_Digit_Display hex_digit_display_3 (.value(ans[7:4]));  // open: dp
  Hex_Digit_Display hex_digit_display_4 (.value(ans[3:0]));  // open: dp
  // Probe on n32reg_1_r1
  // Probe on alu_1_result
  // Probe on ans
endmodule
